// Logisim project Combination_Logic_Circuit.circ as structural Verilog: 26 circuits, main circuit Decoder_2_4
module Hex_Dec_7_segment_display (
  input  S
);

  wire [3:0] and_1_out, and_2_out, dipswitch_1_p1, not_1_out;
  wire [6:0] and_3_out, and_4_out, decimal_7_segment_decoder_1_out_1, hex_7_segment_decoder_1_out_1, or_1_out;
  wire [6:6] not_2_out;

  // DipSwitch #(.number(4)) dipswitch_1: pin names not known; wires that end beside it: dipswitch_1_p1[0], dipswitch_1_p1[1], dipswitch_1_p1[2], dipswitch_1_p1[3]
  assign not_1_out = ~{4{S}};  // NOT_Gate not_1, 4 bits wide
  assign and_1_out = dipswitch_1_p1 & not_1_out;  // AND_Gate and_1, 4 bits wide
  assign and_2_out = dipswitch_1_p1 & {4{S}};  // AND_Gate and_2, 4 bits wide
  Hex_7_segment_decoder hex_7_segment_decoder_1 (
    .in_1(and_1_out[0]), .in_2(and_1_out[1]), .in_3(and_1_out[2]), .in_4(and_1_out[3]),
    .Out_1(hex_7_segment_decoder_1_out_1[0]), .Out_2(hex_7_segment_decoder_1_out_1[1]),
    .Out_3(hex_7_segment_decoder_1_out_1[2]), .Out_4(hex_7_segment_decoder_1_out_1[3]),
    .Out_5(hex_7_segment_decoder_1_out_1[4]), .Out_6(hex_7_segment_decoder_1_out_1[5]),
    .Out_7(hex_7_segment_decoder_1_out_1[6]));
  Decimal_7_segment_decoder decimal_7_segment_decoder_1 (
    .In_0(and_2_out[0]), .In_1(and_2_out[1]), .In_2(and_2_out[2]), .In_3(and_2_out[3]),
    .Out_1(decimal_7_segment_decoder_1_out_1[0]), .Out_2(decimal_7_segment_decoder_1_out_1[1]),
    .Out_3(decimal_7_segment_decoder_1_out_1[2]), .Out_4(decimal_7_segment_decoder_1_out_1[3]),
    .Out_5(decimal_7_segment_decoder_1_out_1[4]), .Out_6(decimal_7_segment_decoder_1_out_1[5]),
    .Out_7(decimal_7_segment_decoder_1_out_1[6]));
  not not_2 (not_2_out[6], S);
  assign and_3_out = {7{not_2_out[6]}} & hex_7_segment_decoder_1_out_1;  // AND_Gate and_3, 7 bits wide
  assign and_4_out = decimal_7_segment_decoder_1_out_1 & {7{S}};  // AND_Gate and_4, 7 bits wide
  assign or_1_out = and_3_out | and_4_out;  // OR_Gate or_1, 7 bits wide
  _7_Segment_Display u_7_segment_display_1 (
    .g(or_1_out[0]), .f(or_1_out[1]), .a(or_1_out[2]), .b(or_1_out[3]), .e(or_1_out[4]), .d(or_1_out[5]),
    .c(or_1_out[6]));  // open: dp
endmodule

module Decoder_2_4 (
  input  In_0,
  input  In_1,
  output Out_0,
  output Out_1,
  output Out_2,
  output Out_3
);

  wire not_1_out, not_2_out;

  not not_1 (not_1_out, In_1);
  not not_2 (not_2_out, In_0);
  nor nor_1 (Out_0, In_1, In_0);
  and and_1 (Out_1, not_1_out, In_0);
  and and_2 (Out_2, In_1, not_2_out);
  and and_3 (Out_3, In_1, In_0);
endmodule

module Decoder_3_8 (
  input  in_1,
  input  in_2,
  input  in_3,
  output Out_0,
  output Out_1,
  output Out_2,
  output Out_3,
  output Out_4,
  output Out_5,
  output Out_6,
  output Out_7
);

  wire and_1_out, decoder_2_4_3_out_0, decoder_2_4_3_out_1, decoder_2_4_3_out_2, decoder_2_4_3_out_3,
       decoder_2_4_4_out_0, decoder_2_4_4_out_1, not_1_out, undriven;
  wire [3:0] controlled_buffer_1_out, controlled_buffer_2_out, decoder_2_4_5_out_0;
  wire [7:3] decoder_2_4_2_out_0;
  wire [7:4] decoder_2_4_1_out_0;

  Decoder_2_4 decoder_2_4_1 (
    .In_0(in_1), .In_1(in_2), .Out_0(decoder_2_4_1_out_0[4]), .Out_1(decoder_2_4_1_out_0[5]),
    .Out_2(decoder_2_4_1_out_0[6]), .Out_3(decoder_2_4_1_out_0[7]));
  Decoder_2_4 decoder_2_4_2 (
    .In_0(in_3), .Out_0(decoder_2_4_2_out_0[3]), .Out_1(decoder_2_4_2_out_0[7]));  // open: In_1, Out_2, Out_3
  Decoder_2_4 decoder_2_4_3 (
    .Out_0(decoder_2_4_3_out_0), .Out_1(decoder_2_4_3_out_1), .Out_2(decoder_2_4_3_out_2),
    .Out_3(decoder_2_4_3_out_3));  // open: In_0, In_1
  Decoder_2_4 decoder_2_4_4 (
    .Out_0(decoder_2_4_4_out_0), .Out_1(decoder_2_4_4_out_1));  // open: In_0, In_1, Out_2, Out_3
  and and_1 (and_1_out, decoder_2_4_3_out_0, decoder_2_4_4_out_0);
  // AND_Gate and_2 has open pins: in0=decoder_2_4_3_out_1, in1=decoder_2_4_4_out_0, out=open
  // AND_Gate and_3 has open pins: in0=decoder_2_4_3_out_2, in1=decoder_2_4_4_out_0, out=open
  // AND_Gate and_4 has open pins: in0=decoder_2_4_3_out_3, in1=decoder_2_4_4_out_0, out=open
  // AND_Gate and_5 has open pins: in0=decoder_2_4_3_out_0, in1=decoder_2_4_4_out_1, out=open
  // AND_Gate and_6 has open pins: in0=decoder_2_4_3_out_1, in1=decoder_2_4_4_out_1, out=open
  // AND_Gate and_7 has open pins: in0=decoder_2_4_3_out_2, in1=decoder_2_4_4_out_1, out=open
  // AND_Gate and_8 has open pins: in0=decoder_2_4_3_out_3, in1=decoder_2_4_4_out_1, out=open
  assign {Out_7, Out_6, Out_5, Out_4, Out_3, Out_2, Out_1, Out_0} = {decoder_2_4_1_out_0, decoder_2_4_1_out_0} & {{4{decoder_2_4_2_out_0[7]}}, {4{decoder_2_4_2_out_0[3]}}};  // AND_Gate and_9, 8 bits wide
  Decoder_2_4 decoder_2_4_5 (
    .Out_0(decoder_2_4_5_out_0[0]), .Out_1(decoder_2_4_5_out_0[1]), .Out_2(decoder_2_4_5_out_0[2]),
    .Out_3(decoder_2_4_5_out_0[3]));  // open: In_0, In_1
  not not_1 (not_1_out, undriven);
  assign controlled_buffer_1_out = not_1_out ? decoder_2_4_5_out_0 : 4'bz;  // Controlled_Buffer controlled_buffer_1
  assign controlled_buffer_2_out = undriven ? decoder_2_4_5_out_0 : 4'bz;  // Controlled_Buffer controlled_buffer_2
endmodule

module Decimal_7_segment_decoder (
  input  In_0,
  input  In_1,
  input  In_2,
  input  In_3,
  output Out_1,
  output Out_2,
  output Out_3,
  output Out_4,
  output Out_5,
  output Out_6,
  output Out_7
);

  wire decoder_4_16_1_out_0, decoder_4_16_1_out_1, decoder_4_16_1_out_2, decoder_4_16_1_out_3,
       decoder_4_16_1_out_4, decoder_4_16_1_out_5, decoder_4_16_1_out_6, decoder_4_16_1_out_7,
       decoder_4_16_1_out_8, decoder_4_16_1_out_9;

  Decoder_4_16 decoder_4_16_1 (
    .In_0(In_0), .In_1(In_1), .In_2(In_2), .In_3(In_3), .Out_0(decoder_4_16_1_out_0),
    .Out_1(decoder_4_16_1_out_1), .Out_2(decoder_4_16_1_out_2), .Out_3(decoder_4_16_1_out_3),
    .Out_4(decoder_4_16_1_out_4), .Out_5(decoder_4_16_1_out_5), .Out_6(decoder_4_16_1_out_6),
    .Out_7(decoder_4_16_1_out_7), .Out_8(decoder_4_16_1_out_8), .Out_9(decoder_4_16_1_out_9));  // open: Out_10, Out_11, Out_12, Out_13, Out_14, Out_15
  or or_1 (Out_1, decoder_4_16_1_out_2, decoder_4_16_1_out_3, decoder_4_16_1_out_4, decoder_4_16_1_out_5, decoder_4_16_1_out_6, decoder_4_16_1_out_8, decoder_4_16_1_out_9);
  or or_2 (Out_2, decoder_4_16_1_out_0, decoder_4_16_1_out_4, decoder_4_16_1_out_5, decoder_4_16_1_out_6, decoder_4_16_1_out_8, decoder_4_16_1_out_9);
  or or_3 (Out_3, decoder_4_16_1_out_0, decoder_4_16_1_out_2, decoder_4_16_1_out_3, decoder_4_16_1_out_5, decoder_4_16_1_out_6, decoder_4_16_1_out_7, decoder_4_16_1_out_8, decoder_4_16_1_out_9);
  or or_4 (Out_4, decoder_4_16_1_out_0, decoder_4_16_1_out_1, decoder_4_16_1_out_2, decoder_4_16_1_out_3, decoder_4_16_1_out_4, decoder_4_16_1_out_7, decoder_4_16_1_out_8, decoder_4_16_1_out_9);
  or or_5 (Out_5, decoder_4_16_1_out_0, decoder_4_16_1_out_2, decoder_4_16_1_out_6, decoder_4_16_1_out_8);
  or or_6 (Out_6, decoder_4_16_1_out_0, decoder_4_16_1_out_2, decoder_4_16_1_out_3, decoder_4_16_1_out_5, decoder_4_16_1_out_6, decoder_4_16_1_out_8, decoder_4_16_1_out_9);
  or or_7 (Out_7, decoder_4_16_1_out_0, decoder_4_16_1_out_1, decoder_4_16_1_out_3, decoder_4_16_1_out_4, decoder_4_16_1_out_5, decoder_4_16_1_out_6, decoder_4_16_1_out_7, decoder_4_16_1_out_8, decoder_4_16_1_out_9);
  _7_Segment_Display u_7_segment_display_1 ();  // open: g, f, a, b, e, d, c, dp
endmodule

module Decoder_4_16 (
  input  In_0,
  input  In_1,
  input  In_2,
  input  In_3,
  output Out_0,
  output Out_1,
  output Out_2,
  output Out_3,
  output Out_4,
  output Out_5,
  output Out_6,
  output Out_7,
  output Out_8,
  output Out_9,
  output Out_10,
  output Out_11,
  output Out_12,
  output Out_13,
  output Out_14,
  output Out_15
);

  wire [15:7] decoder_3_8_2_out_0;
  wire [15:8] decoder_3_8_1_out_0;

  Decoder_3_8 decoder_3_8_1 (
    .in_1(In_0), .in_2(In_1), .in_3(In_2), .Out_0(decoder_3_8_1_out_0[8]), .Out_1(decoder_3_8_1_out_0[9]),
    .Out_2(decoder_3_8_1_out_0[10]), .Out_3(decoder_3_8_1_out_0[11]), .Out_4(decoder_3_8_1_out_0[12]),
    .Out_5(decoder_3_8_1_out_0[13]), .Out_6(decoder_3_8_1_out_0[14]), .Out_7(decoder_3_8_1_out_0[15]));
  Decoder_3_8 decoder_3_8_2 (
    .in_1(In_3), .Out_0(decoder_3_8_2_out_0[7]), .Out_1(decoder_3_8_2_out_0[15]));  // open: in_2, in_3, Out_2, Out_3, Out_4, Out_5, Out_6, Out_7
  assign {Out_15, Out_14, Out_13, Out_12, Out_11, Out_10, Out_9, Out_8, Out_7, Out_6, Out_5, Out_4, Out_3, Out_2, Out_1, Out_0} = {decoder_3_8_1_out_0, decoder_3_8_1_out_0} & {{8{decoder_3_8_2_out_0[15]}}, {8{decoder_3_8_2_out_0[7]}}};  // AND_Gate and_1, 16 bits wide
endmodule

module Hex_7_segment_decoder (
  input  in_1,
  input  in_2,
  input  in_3,
  input  in_4,
  output Out_1,
  output Out_2,
  output Out_3,
  output Out_4,
  output Out_5,
  output Out_6,
  output Out_7
);

  wire decoder_4_16_1_out_0, decoder_4_16_1_out_1, decoder_4_16_1_out_2, decoder_4_16_1_out_3,
       decoder_4_16_1_out_4, decoder_4_16_1_out_5, decoder_4_16_1_out_6, decoder_4_16_1_out_7,
       decoder_4_16_1_out_8, decoder_4_16_1_out_9, decoder_4_16_1_out_10, decoder_4_16_1_out_11,
       decoder_4_16_1_out_12, decoder_4_16_1_out_13, decoder_4_16_1_out_14, decoder_4_16_1_out_15;

  Decoder_4_16 decoder_4_16_1 (
    .In_0(in_1), .In_1(in_2), .In_2(in_3), .In_3(in_4), .Out_0(decoder_4_16_1_out_0),
    .Out_1(decoder_4_16_1_out_1), .Out_2(decoder_4_16_1_out_2), .Out_3(decoder_4_16_1_out_3),
    .Out_4(decoder_4_16_1_out_4), .Out_5(decoder_4_16_1_out_5), .Out_6(decoder_4_16_1_out_6),
    .Out_7(decoder_4_16_1_out_7), .Out_8(decoder_4_16_1_out_8), .Out_9(decoder_4_16_1_out_9),
    .Out_10(decoder_4_16_1_out_10), .Out_11(decoder_4_16_1_out_11), .Out_12(decoder_4_16_1_out_12),
    .Out_13(decoder_4_16_1_out_13), .Out_14(decoder_4_16_1_out_14), .Out_15(decoder_4_16_1_out_15));
  or or_1 (Out_1, decoder_4_16_1_out_2, decoder_4_16_1_out_3, decoder_4_16_1_out_4, decoder_4_16_1_out_5, decoder_4_16_1_out_6, decoder_4_16_1_out_8, decoder_4_16_1_out_9, decoder_4_16_1_out_10, decoder_4_16_1_out_11, decoder_4_16_1_out_13, decoder_4_16_1_out_14, decoder_4_16_1_out_15);
  or or_2 (Out_2, decoder_4_16_1_out_0, decoder_4_16_1_out_4, decoder_4_16_1_out_5, decoder_4_16_1_out_6, decoder_4_16_1_out_8, decoder_4_16_1_out_9, decoder_4_16_1_out_10, decoder_4_16_1_out_11, decoder_4_16_1_out_12, decoder_4_16_1_out_14, decoder_4_16_1_out_15);
  or or_3 (Out_3, decoder_4_16_1_out_0, decoder_4_16_1_out_2, decoder_4_16_1_out_3, decoder_4_16_1_out_5, decoder_4_16_1_out_6, decoder_4_16_1_out_7, decoder_4_16_1_out_8, decoder_4_16_1_out_9, decoder_4_16_1_out_10, decoder_4_16_1_out_12, decoder_4_16_1_out_14, decoder_4_16_1_out_15);
  or or_4 (Out_4, decoder_4_16_1_out_0, decoder_4_16_1_out_1, decoder_4_16_1_out_2, decoder_4_16_1_out_3, decoder_4_16_1_out_4, decoder_4_16_1_out_7, decoder_4_16_1_out_8, decoder_4_16_1_out_9, decoder_4_16_1_out_10, decoder_4_16_1_out_13);
  or or_5 (Out_5, decoder_4_16_1_out_0, decoder_4_16_1_out_2, decoder_4_16_1_out_6, decoder_4_16_1_out_8, decoder_4_16_1_out_10, decoder_4_16_1_out_11, decoder_4_16_1_out_12, decoder_4_16_1_out_13, decoder_4_16_1_out_14, decoder_4_16_1_out_15);
  or or_6 (Out_6, decoder_4_16_1_out_0, decoder_4_16_1_out_2, decoder_4_16_1_out_3, decoder_4_16_1_out_5, decoder_4_16_1_out_6, decoder_4_16_1_out_8, decoder_4_16_1_out_9, decoder_4_16_1_out_11, decoder_4_16_1_out_12, decoder_4_16_1_out_13, decoder_4_16_1_out_14);
  or or_7 (Out_7, decoder_4_16_1_out_0, decoder_4_16_1_out_1, decoder_4_16_1_out_3, decoder_4_16_1_out_4, decoder_4_16_1_out_5, decoder_4_16_1_out_6, decoder_4_16_1_out_7, decoder_4_16_1_out_8, decoder_4_16_1_out_9, decoder_4_16_1_out_10, decoder_4_16_1_out_11, decoder_4_16_1_out_13);
  _7_Segment_Display u_7_segment_display_1 ();  // open: g, f, a, b, e, d, c, dp
endmodule

module Encoder_16_4 (
  input  In_0000,
  input  In_0001,
  input  In_0010,
  input  In_0011,
  input  In_0100,
  input  In_0101,
  input  In_0110,
  input  In_0111,
  input  In_1000,
  input  In_1001,
  input  In_1010,
  input  In_1011,
  input  In_1100,
  input  In_1101,
  input  In_1110,
  input  In_1111,
  output Out_0,
  output Out_1,
  output Out_2,
  output Out_3
);

  or or_1 (Out_0, In_0001, In_0011, In_0101, In_0111, In_1001, In_1011, In_1101, In_1111);
  or or_2 (Out_1, In_0010, In_0011, In_0110, In_0111, In_1010, In_1011, In_1110, In_1111);
  or or_3 (Out_2, In_0100, In_0101, In_0110, In_0111, In_1100, In_1101, In_1110, In_1111);
  or or_4 (Out_3, In_1000, In_1001, In_1010, In_1011, In_1100, In_1101, In_1110, In_1111);
endmodule

module Priority_encoder_4_2 (
  input  In_0,
  input  In_1,
  input  In_2,
  input  In_3,
  output Out_0,
  output Out_1
);

  wire and_1_out, not_1_out;

  not not_1 (not_1_out, In_2);
  or or_1 (Out_0, In_3, and_1_out);
  and and_1 (and_1_out, In_1, not_1_out);
  or or_2 (Out_1, In_3, In_2);
endmodule

module Priority_encoder_8_3 (
  input  In_00,
  input  In_01,
  input  In_10,
  input  In_11,
  input  In_100,
  input  In_101,
  input  In_110,
  input  In_111,
  output O0,
  output O1,
  output O2
);

  wire and_1_out, and_2_out, not_1_out, priority_encoder_4_2_1_out_0, priority_encoder_4_2_1_out_1,
       priority_encoder_4_2_2_out_0, priority_encoder_4_2_2_out_1;

  Priority_encoder_4_2 priority_encoder_4_2_1 (
    .In_0(In_00), .In_1(In_01), .In_2(In_10), .In_3(In_11), .Out_0(priority_encoder_4_2_1_out_0),
    .Out_1(priority_encoder_4_2_1_out_1));
  Priority_encoder_4_2 priority_encoder_4_2_2 (
    .In_0(In_100), .In_1(In_101), .In_2(In_110), .In_3(In_111), .Out_0(priority_encoder_4_2_2_out_0),
    .Out_1(priority_encoder_4_2_2_out_1));
  not not_1 (not_1_out, O2);
  or or_1 (O2, In_100, priority_encoder_4_2_2_out_0, priority_encoder_4_2_2_out_1);
  and and_1 (and_1_out, priority_encoder_4_2_1_out_0, not_1_out);
  and and_2 (and_2_out, priority_encoder_4_2_1_out_1, not_1_out);
  or or_2 (O0, and_1_out, priority_encoder_4_2_2_out_0);
  or or_3 (O1, and_2_out, priority_encoder_4_2_2_out_1);
endmodule

module Priority_encoder_16_4 (
  input  in_1,
  input  in_2,
  input  in_3,
  input  in_4,
  input  in_5,
  input  in_6,
  input  in_7,
  input  in_8,
  input  in_9,
  input  in_10,
  input  in_11,
  input  in_12,
  input  in_13,
  input  in_14,
  input  in_15,
  input  in_16,
  output Out_0,
  output Out_1,
  output Out_2,
  output Out_3
);

  wire and_1_out, and_2_out, and_3_out, not_1_out, priority_encoder_8_3_1_o0, priority_encoder_8_3_1_o1,
       priority_encoder_8_3_1_o2, priority_encoder_8_3_2_o0, priority_encoder_8_3_2_o1,
       priority_encoder_8_3_2_o2;

  Priority_encoder_8_3 priority_encoder_8_3_1 (
    .In_00(in_1), .In_01(in_2), .In_10(in_3), .In_11(in_4), .In_100(in_5), .In_101(in_6), .In_110(in_7),
    .In_111(in_8), .O0(priority_encoder_8_3_1_o0), .O1(priority_encoder_8_3_1_o1),
    .O2(priority_encoder_8_3_1_o2));
  Priority_encoder_8_3 priority_encoder_8_3_2 (
    .In_00(in_9), .In_01(in_10), .In_10(in_11), .In_11(in_12), .In_100(in_13), .In_101(in_14),
    .In_110(in_15), .In_111(in_16), .O0(priority_encoder_8_3_2_o0), .O1(priority_encoder_8_3_2_o1),
    .O2(priority_encoder_8_3_2_o2));
  or or_1 (Out_3, priority_encoder_8_3_2_o0, priority_encoder_8_3_2_o1, priority_encoder_8_3_2_o2, in_9);
  not not_1 (not_1_out, Out_3);
  and and_1 (and_1_out, priority_encoder_8_3_1_o0, not_1_out);
  and and_2 (and_2_out, priority_encoder_8_3_1_o1, not_1_out);
  and and_3 (and_3_out, priority_encoder_8_3_1_o2, not_1_out);
  or or_2 (Out_0, and_1_out, priority_encoder_8_3_2_o0);
  or or_3 (Out_1, and_2_out, priority_encoder_8_3_2_o1);
  or or_4 (Out_2, and_3_out, priority_encoder_8_3_2_o2);
endmodule

module Seven_segment_display_circuit (
);

  wire dipswitch_1_p1, dipswitch_1_p2, dipswitch_1_p3, dipswitch_1_p4, dipswitch_1_p5, dipswitch_1_p6,
       dipswitch_1_p7, dipswitch_1_p8, dipswitch_1_p9, dipswitch_1_p10, dipswitch_1_p11, dipswitch_1_p12,
       dipswitch_1_p13, dipswitch_1_p14, dipswitch_1_p15, dipswitch_1_p16, hex_7_segment_decoder_1_out_1,
       hex_7_segment_decoder_1_out_2, hex_7_segment_decoder_1_out_3, hex_7_segment_decoder_1_out_4,
       hex_7_segment_decoder_1_out_5, hex_7_segment_decoder_1_out_6, hex_7_segment_decoder_1_out_7,
       priority_encoder_16_4_1_out_0, priority_encoder_16_4_1_out_1, priority_encoder_16_4_1_out_2,
       priority_encoder_16_4_1_out_3;

  // DipSwitch #(.number(16)) dipswitch_1: pin names not known; wires that end beside it: dipswitch_1_p1, dipswitch_1_p2, dipswitch_1_p3, dipswitch_1_p4, dipswitch_1_p5, dipswitch_1_p6, dipswitch_1_p7, dipswitch_1_p8, dipswitch_1_p9, dipswitch_1_p10, dipswitch_1_p11, dipswitch_1_p12, dipswitch_1_p13, dipswitch_1_p14, dipswitch_1_p15, dipswitch_1_p16
  Priority_encoder_16_4 priority_encoder_16_4_1 (
    .in_1(dipswitch_1_p1), .in_2(dipswitch_1_p2), .in_3(dipswitch_1_p3), .in_4(dipswitch_1_p4),
    .in_5(dipswitch_1_p5), .in_6(dipswitch_1_p6), .in_7(dipswitch_1_p7), .in_8(dipswitch_1_p8),
    .in_9(dipswitch_1_p9), .in_10(dipswitch_1_p10), .in_11(dipswitch_1_p11), .in_12(dipswitch_1_p12),
    .in_13(dipswitch_1_p13), .in_14(dipswitch_1_p14), .in_15(dipswitch_1_p15), .in_16(dipswitch_1_p16),
    .Out_0(priority_encoder_16_4_1_out_0), .Out_1(priority_encoder_16_4_1_out_1),
    .Out_2(priority_encoder_16_4_1_out_2), .Out_3(priority_encoder_16_4_1_out_3));
  Hex_7_segment_decoder hex_7_segment_decoder_1 (
    .in_1(priority_encoder_16_4_1_out_0), .in_2(priority_encoder_16_4_1_out_1),
    .in_3(priority_encoder_16_4_1_out_2), .in_4(priority_encoder_16_4_1_out_3),
    .Out_1(hex_7_segment_decoder_1_out_1), .Out_2(hex_7_segment_decoder_1_out_2),
    .Out_3(hex_7_segment_decoder_1_out_3), .Out_4(hex_7_segment_decoder_1_out_4),
    .Out_5(hex_7_segment_decoder_1_out_5), .Out_6(hex_7_segment_decoder_1_out_6),
    .Out_7(hex_7_segment_decoder_1_out_7));
  _7_Segment_Display u_7_segment_display_1 (
    .g(hex_7_segment_decoder_1_out_1), .f(hex_7_segment_decoder_1_out_2), .a(hex_7_segment_decoder_1_out_3),
    .b(hex_7_segment_decoder_1_out_4), .e(hex_7_segment_decoder_1_out_5), .d(hex_7_segment_decoder_1_out_6),
    .c(hex_7_segment_decoder_1_out_7));  // open: dp
endmodule

module Multiplexer_3_bit_2_to_1 (
  input  A0,
  input  A1,
  input  A2,
  input  B0,
  input  B1,
  input  B2,
  input  S,
  output Out1,
  output Out2,
  output Out3
);

  wire [2:0] and_1_out, and_2_out;
  wire [2:2] not_1_out;

  not not_1 (not_1_out[2], S);
  assign and_1_out = {A2, A1, A0} & {3{S}};  // AND_Gate and_1, 3 bits wide
  assign and_2_out = {3{not_1_out[2]}} & {B2, B1, B0};  // AND_Gate and_2, 3 bits wide
  assign {Out3, Out2, Out1} = and_1_out | and_2_out;  // OR_Gate or_1, 3 bits wide
endmodule

module Multiplexer_3_bit_4_to_1 (
  input  in_1,
  input  in_2,
  input  in_3,
  input  in_4,
  input  in_5,
  input  in_6,
  input  S1,
  input  S2,
  input  in_9,
  input  in_10,
  input  in_11,
  input  in_12,
  input  in_13,
  input  in_14,
  output out_15,
  output out_16,
  output out_17
);

  wire [2:0] and_1_out, and_2_out, and_3_out, and_4_out;
  wire [2:2] decoder_2_4_1_out_0, decoder_2_4_1_out_1, decoder_2_4_1_out_2, decoder_2_4_1_out_3;

  Decoder_2_4 decoder_2_4_1 (
    .In_0(S1), .In_1(S2), .Out_0(decoder_2_4_1_out_0[2]), .Out_1(decoder_2_4_1_out_1[2]),
    .Out_2(decoder_2_4_1_out_2[2]), .Out_3(decoder_2_4_1_out_3[2]));
  assign and_1_out = {in_3, in_2, in_1} & {3{decoder_2_4_1_out_0[2]}};  // AND_Gate and_1, 3 bits wide
  assign and_2_out = {in_6, in_5, in_4} & {3{decoder_2_4_1_out_1[2]}};  // AND_Gate and_2, 3 bits wide
  assign and_3_out = {3{decoder_2_4_1_out_2[2]}} & {in_11, in_10, in_9};  // AND_Gate and_3, 3 bits wide
  assign and_4_out = {3{decoder_2_4_1_out_3[2]}} & {in_14, in_13, in_12};  // AND_Gate and_4, 3 bits wide
  assign {out_17, out_16, out_15} = and_1_out | and_2_out | and_3_out | and_4_out;  // OR_Gate or_1, 3 bits wide
endmodule

module Comparator_4_bit (
);

  wire and_1_out, dipswitch_1_p1, dipswitch_1_p2, dipswitch_1_p3, dipswitch_2_p1, dipswitch_2_p2,
       dipswitch_2_p3, dipswitch_2_p4, dipswitch_2_p5, xnor_1_out, xnor_2_out, xnor_3_out, xnor_4_out;

  // DipSwitch #(.number(4)) dipswitch_1: pin names not known; wires that end beside it: dipswitch_1_p1, dipswitch_1_p2, dipswitch_1_p3
  // DipSwitch #(.number(4)) dipswitch_2: pin names not known; wires that end beside it: dipswitch_2_p1, dipswitch_2_p2, dipswitch_2_p3, dipswitch_2_p4, dipswitch_2_p5
  xnor xnor_1 (xnor_1_out, dipswitch_1_p1, dipswitch_2_p2);
  xnor xnor_2 (xnor_2_out, dipswitch_1_p2, dipswitch_2_p3);
  xnor xnor_3 (xnor_3_out, dipswitch_1_p3, dipswitch_2_p4);
  xnor xnor_4 (xnor_4_out, dipswitch_2_p1, dipswitch_2_p5);
  and and_1 (and_1_out, xnor_1_out, xnor_2_out, xnor_3_out, xnor_4_out);
  LED led_1 (.in(and_1_out));
endmodule

module Comparator_8_bit (
  input  A0,
  input  A1,
  input  A2,
  input  A3,
  input  A4,
  input  A5,
  input  A6,
  input  A7,
  input  B0,
  input  B1,
  input  B2,
  input  B3,
  input  B4,
  input  B5,
  input  B6,
  input  B7,
  output out_17
);

  wire [7:0] xnor_1_out;

  assign xnor_1_out = ~({A7, A6, A5, A4, A3, A2, A1, A0} ^ {B7, B6, B5, B4, B3, B2, B1, B0});  // XNOR_Gate xnor_1, 8 bits wide
  and and_1 (out_17, xnor_1_out[0], xnor_1_out[1], xnor_1_out[2], xnor_1_out[3], xnor_1_out[4], xnor_1_out[5], xnor_1_out[6], xnor_1_out[7]);
endmodule

module Full_Adder_half_adder_based (
  input  A1,
  input  B1,
  input  Cin1,
  output S1,
  output Cout1
);

  wire half_adder_1_c, half_adder_1_s, half_adder_2_c;

  Half_adder half_adder_1 (.A(A1), .B(B1), .S(half_adder_1_s), .C(half_adder_1_c));
  Half_adder half_adder_2 (.A(half_adder_1_s), .B(Cin1), .S(S1), .C(half_adder_2_c));
  or or_1 (Cout1, half_adder_2_c, half_adder_1_c);
endmodule

module Full_Adder_gates_based (
  input  A,
  input  B,
  input  Cin,
  output S,
  output Cout
);

  wire and_1_out, and_2_out, or_1_out, xor_1_out;

  or or_1 (or_1_out, B, Cin);
  and and_1 (and_1_out, B, Cin);
  and and_2 (and_2_out, A, or_1_out);
  xor xor_1 (xor_1_out, A, B);
  or or_2 (Cout, and_2_out, and_1_out);
  xor xor_2 (S, xor_1_out, Cin);
endmodule

module Half_adder (
  input  A,
  input  B,
  output S,
  output C
);

  xor xor_1 (S, A, B);
  and and_1 (C, A, B);
endmodule

module Four_bit_Adder (
  input  A0,
  input  A1,
  input  A2,
  input  A3,
  input  B0,
  input  B1,
  input  B2,
  input  B3,
  output Cn,
  output Out1,
  output Out2,
  output Out3,
  output Out4,
  output Cout
);

  wire full_adder_half_adder_based_1_cout1, full_adder_half_adder_based_2_cout1,
       hex_7_segment_decoder_1_out_1, hex_7_segment_decoder_1_out_2, hex_7_segment_decoder_1_out_3,
       hex_7_segment_decoder_1_out_4, hex_7_segment_decoder_1_out_5, hex_7_segment_decoder_1_out_6,
       hex_7_segment_decoder_1_out_7, hex_7_segment_decoder_2_out_1, hex_7_segment_decoder_2_out_2,
       hex_7_segment_decoder_2_out_3, hex_7_segment_decoder_2_out_4, hex_7_segment_decoder_2_out_5,
       hex_7_segment_decoder_2_out_6, hex_7_segment_decoder_2_out_7;

  Hex_7_segment_decoder hex_7_segment_decoder_1 (
    .in_1(A0), .in_2(A1), .in_3(A2), .in_4(A3), .Out_1(hex_7_segment_decoder_1_out_1),
    .Out_2(hex_7_segment_decoder_1_out_2), .Out_3(hex_7_segment_decoder_1_out_3),
    .Out_4(hex_7_segment_decoder_1_out_4), .Out_5(hex_7_segment_decoder_1_out_5),
    .Out_6(hex_7_segment_decoder_1_out_6), .Out_7(hex_7_segment_decoder_1_out_7));
  Hex_7_segment_decoder hex_7_segment_decoder_2 (
    .in_1(B0), .in_2(B1), .in_3(B2), .in_4(B3), .Out_1(hex_7_segment_decoder_2_out_1),
    .Out_2(hex_7_segment_decoder_2_out_2), .Out_3(hex_7_segment_decoder_2_out_3),
    .Out_4(hex_7_segment_decoder_2_out_4), .Out_5(hex_7_segment_decoder_2_out_5),
    .Out_6(hex_7_segment_decoder_2_out_6), .Out_7(hex_7_segment_decoder_2_out_7));
  Full_Adder_half_adder_based full_adder_half_adder_based_1 (
    .A1(A0), .B1(B0), .Cin1(1'b0), .S1(Out1), .Cout1(full_adder_half_adder_based_1_cout1));
  _7_Segment_Display u_7_segment_display_1 (
    .g(hex_7_segment_decoder_2_out_1), .f(hex_7_segment_decoder_2_out_2), .a(hex_7_segment_decoder_2_out_3),
    .b(hex_7_segment_decoder_2_out_4), .e(hex_7_segment_decoder_2_out_5), .d(hex_7_segment_decoder_2_out_6),
    .c(hex_7_segment_decoder_2_out_7));  // open: dp
  _7_Segment_Display u_7_segment_display_2 (
    .g(hex_7_segment_decoder_1_out_1), .f(hex_7_segment_decoder_1_out_2), .a(hex_7_segment_decoder_1_out_3),
    .b(hex_7_segment_decoder_1_out_4), .e(hex_7_segment_decoder_1_out_5), .d(hex_7_segment_decoder_1_out_6),
    .c(hex_7_segment_decoder_1_out_7));  // open: dp
  Full_Adder_half_adder_based full_adder_half_adder_based_2 (
    .A1(A1), .B1(B1), .Cin1(full_adder_half_adder_based_1_cout1), .S1(Out2),
    .Cout1(full_adder_half_adder_based_2_cout1));
  Full_Adder_half_adder_based full_adder_half_adder_based_3 (
    .A1(A2), .B1(B2), .Cin1(full_adder_half_adder_based_2_cout1), .S1(Out3), .Cout1(Cn));
  Hex_7_segment_decoder hex_7_segment_decoder_3 ();  // open: in_1, in_2, in_3, in_4, Out_1, Out_2, Out_3, Out_4, Out_5, Out_6, Out_7
  Full_Adder_half_adder_based full_adder_half_adder_based_4 (.A1(A3), .B1(B3), .Cin1(Cn), .S1(Out4), .Cout1(Cout));
endmodule

module Eight_bit_Adder (
  input  A0,
  input  A1,
  input  A2,
  input  A3,
  input  A4,
  input  A5,
  input  A6,
  input  A7,
  input  B0,
  input  B1,
  input  B2,
  input  B3,
  input  B4,
  input  B5,
  input  B6,
  input  B7,
  output Out1,
  output Out2,
  output Out3,
  output Out4,
  output Out5,
  output Out6,
  output Out7,
  output Out8,
  output Cn,
  output Cout
);

  wire full_adder_half_adder_based_1_cout1, full_adder_half_adder_based_2_cout1,
       full_adder_half_adder_based_3_cout1, full_adder_half_adder_based_4_cout1,
       full_adder_half_adder_based_5_cout1, full_adder_half_adder_based_6_cout1;

  Full_Adder_half_adder_based full_adder_half_adder_based_1 (
    .A1(A0), .B1(B0), .Cin1(1'b0), .S1(Out1), .Cout1(full_adder_half_adder_based_1_cout1));
  Full_Adder_half_adder_based full_adder_half_adder_based_2 (
    .A1(A1), .B1(B1), .Cin1(full_adder_half_adder_based_1_cout1), .S1(Out2),
    .Cout1(full_adder_half_adder_based_2_cout1));
  Full_Adder_half_adder_based full_adder_half_adder_based_3 (
    .A1(A2), .B1(B2), .Cin1(full_adder_half_adder_based_2_cout1), .S1(Out3),
    .Cout1(full_adder_half_adder_based_3_cout1));
  Full_Adder_half_adder_based full_adder_half_adder_based_4 (
    .A1(A3), .B1(B3), .Cin1(full_adder_half_adder_based_3_cout1), .S1(Out4),
    .Cout1(full_adder_half_adder_based_4_cout1));
  Full_Adder_half_adder_based full_adder_half_adder_based_5 (
    .A1(A4), .B1(B4), .Cin1(full_adder_half_adder_based_4_cout1), .S1(Out5),
    .Cout1(full_adder_half_adder_based_5_cout1));
  Full_Adder_half_adder_based full_adder_half_adder_based_6 (
    .A1(A5), .B1(B5), .Cin1(full_adder_half_adder_based_5_cout1), .S1(Out6),
    .Cout1(full_adder_half_adder_based_6_cout1));
  Full_Adder_half_adder_based full_adder_half_adder_based_7 (
    .A1(A6), .B1(B6), .Cin1(full_adder_half_adder_based_6_cout1), .S1(Out7), .Cout1(Cn));
  Full_Adder_half_adder_based full_adder_half_adder_based_8 (.A1(A7), .B1(B7), .Cin1(Cn), .S1(Out8), .Cout1(Cout));
endmodule

module Full_subtractor (
  input  A,
  input  B,
  input  Cin,
  output S,
  output Cout
);

  wire and_1_out, and_2_out, not_1_out, or_1_out, xor_1_out;

  xor xor_1 (xor_1_out, A, B);
  not not_1 (not_1_out, A);
  or or_1 (or_1_out, B, Cin);
  and and_1 (and_1_out, not_1_out, or_1_out);
  and and_2 (and_2_out, A, B, Cin);
  xor xor_2 (S, xor_1_out, Cin);
  or or_2 (Cout, and_1_out, and_2_out);
endmodule

module Four_bit_Subtractor (
  input  A0,
  input  A1,
  input  A2,
  input  A3,
  input  B0,
  input  B1,
  input  B2,
  input  B3,
  output Out1,
  output Out2,
  output Out3,
  output Out4,
  output Cout
);

  wire full_subtractor_1_cout, full_subtractor_2_cout, full_subtractor_3_cout, hex_7_segment_decoder_1_out_1,
       hex_7_segment_decoder_1_out_2, hex_7_segment_decoder_1_out_3, hex_7_segment_decoder_1_out_4,
       hex_7_segment_decoder_1_out_5, hex_7_segment_decoder_1_out_6, hex_7_segment_decoder_1_out_7,
       hex_7_segment_decoder_2_out_1, hex_7_segment_decoder_2_out_2, hex_7_segment_decoder_2_out_3,
       hex_7_segment_decoder_2_out_4, hex_7_segment_decoder_2_out_5, hex_7_segment_decoder_2_out_6,
       hex_7_segment_decoder_2_out_7, hex_7_segment_decoder_3_out_1, hex_7_segment_decoder_3_out_2,
       hex_7_segment_decoder_3_out_3, hex_7_segment_decoder_3_out_4, hex_7_segment_decoder_3_out_5,
       hex_7_segment_decoder_3_out_6, hex_7_segment_decoder_3_out_7, undriven;

  Hex_7_segment_decoder hex_7_segment_decoder_1 (
    .in_1(A0), .in_2(A1), .in_3(A2), .in_4(A3), .Out_1(hex_7_segment_decoder_1_out_1),
    .Out_2(hex_7_segment_decoder_1_out_2), .Out_3(hex_7_segment_decoder_1_out_3),
    .Out_4(hex_7_segment_decoder_1_out_4), .Out_5(hex_7_segment_decoder_1_out_5),
    .Out_6(hex_7_segment_decoder_1_out_6), .Out_7(hex_7_segment_decoder_1_out_7));
  Hex_7_segment_decoder hex_7_segment_decoder_2 (
    .in_1(B0), .in_2(B1), .in_3(B2), .in_4(B3), .Out_1(hex_7_segment_decoder_2_out_1),
    .Out_2(hex_7_segment_decoder_2_out_2), .Out_3(hex_7_segment_decoder_2_out_3),
    .Out_4(hex_7_segment_decoder_2_out_4), .Out_5(hex_7_segment_decoder_2_out_5),
    .Out_6(hex_7_segment_decoder_2_out_6), .Out_7(hex_7_segment_decoder_2_out_7));
  _7_Segment_Display u_7_segment_display_1 (
    .g(hex_7_segment_decoder_1_out_1), .f(hex_7_segment_decoder_1_out_2), .a(hex_7_segment_decoder_1_out_3),
    .b(hex_7_segment_decoder_1_out_4), .e(hex_7_segment_decoder_1_out_5), .d(hex_7_segment_decoder_1_out_6),
    .c(hex_7_segment_decoder_1_out_7));  // open: dp
  _7_Segment_Display u_7_segment_display_2 (
    .g(hex_7_segment_decoder_2_out_1), .f(hex_7_segment_decoder_2_out_2), .a(hex_7_segment_decoder_2_out_3),
    .b(hex_7_segment_decoder_2_out_4), .e(hex_7_segment_decoder_2_out_5), .d(hex_7_segment_decoder_2_out_6),
    .c(hex_7_segment_decoder_2_out_7));  // open: dp
  Full_subtractor full_subtractor_1 (.A(A0), .B(B0), .Cin(1'b0), .S(Out1), .Cout(full_subtractor_1_cout));
  Full_subtractor full_subtractor_2 (
    .A(A1), .B(B1), .Cin(full_subtractor_1_cout), .S(Out2), .Cout(full_subtractor_2_cout));
  Full_subtractor full_subtractor_3 (
    .A(A2), .B(B2), .Cin(full_subtractor_2_cout), .S(Out3), .Cout(full_subtractor_3_cout));
  Full_subtractor full_subtractor_4 (.A(A3), .B(B3), .Cin(full_subtractor_3_cout), .S(Out4), .Cout(Cout));
  Hex_7_segment_decoder hex_7_segment_decoder_3 (
    .in_3(undriven), .Out_1(hex_7_segment_decoder_3_out_1), .Out_2(hex_7_segment_decoder_3_out_2),
    .Out_3(hex_7_segment_decoder_3_out_3), .Out_4(hex_7_segment_decoder_3_out_4),
    .Out_5(hex_7_segment_decoder_3_out_5), .Out_6(hex_7_segment_decoder_3_out_6),
    .Out_7(hex_7_segment_decoder_3_out_7));  // open: in_1, in_2, in_4
  _7_Segment_Display u_7_segment_display_3 (
    .g(hex_7_segment_decoder_3_out_1), .f(hex_7_segment_decoder_3_out_2), .a(hex_7_segment_decoder_3_out_3),
    .b(hex_7_segment_decoder_3_out_4), .e(hex_7_segment_decoder_3_out_5), .d(hex_7_segment_decoder_3_out_6),
    .c(hex_7_segment_decoder_3_out_7));  // open: dp
endmodule

module Sign_and_magnitude_Adder (
  input  A0,
  input  A1,
  input  A2,
  input  A3,
  input  B0,
  input  B1,
  input  B2,
  input  B3,
  output Out1,
  output Out2,
  output Out3,
  output Out4,
  output S,
  output Out5,
  output Out6,
  output Out7
);

  wire and_1_out, and_2_out, four_bit_subtractor_1_cout, four_bit_subtractor_2_cout,
       hex_7_segment_decoder_1_out_1, hex_7_segment_decoder_1_out_2, hex_7_segment_decoder_1_out_3,
       hex_7_segment_decoder_1_out_4, hex_7_segment_decoder_1_out_5, hex_7_segment_decoder_1_out_6,
       hex_7_segment_decoder_1_out_7, hex_7_segment_decoder_2_out_1, hex_7_segment_decoder_2_out_2,
       hex_7_segment_decoder_2_out_3, hex_7_segment_decoder_2_out_4, hex_7_segment_decoder_2_out_5,
       hex_7_segment_decoder_2_out_6, hex_7_segment_decoder_2_out_7, xnor_1_out;
  wire [3:0] and_3_out, and_4_out, and_5_out, and_6_out, four_bit_adder_1_out1, four_bit_subtractor_1_out1,
       four_bit_subtractor_2_out1, or_2_out, or_3_out;
  wire [3:3] not_1_out, not_2_out, not_3_out, xnor_2_out;

  Hex_7_segment_decoder hex_7_segment_decoder_1 (
    .in_1(B0), .in_2(B1), .in_3(B2), .in_4(1'b0), .Out_1(hex_7_segment_decoder_1_out_1),
    .Out_2(hex_7_segment_decoder_1_out_2), .Out_3(hex_7_segment_decoder_1_out_3),
    .Out_4(hex_7_segment_decoder_1_out_4), .Out_5(hex_7_segment_decoder_1_out_5),
    .Out_6(hex_7_segment_decoder_1_out_6), .Out_7(hex_7_segment_decoder_1_out_7));
  Hex_7_segment_decoder hex_7_segment_decoder_2 (
    .in_1(A0), .in_2(A1), .in_3(A2), .in_4(1'b0), .Out_1(hex_7_segment_decoder_2_out_1),
    .Out_2(hex_7_segment_decoder_2_out_2), .Out_3(hex_7_segment_decoder_2_out_3),
    .Out_4(hex_7_segment_decoder_2_out_4), .Out_5(hex_7_segment_decoder_2_out_5),
    .Out_6(hex_7_segment_decoder_2_out_6), .Out_7(hex_7_segment_decoder_2_out_7));
  _7_Segment_Display u_7_segment_display_1 (.g(A3));  // open: f, a, b, e, d, c, dp
  _7_Segment_Display u_7_segment_display_2 (.g(B3));  // open: f, a, b, e, d, c, dp
  _7_Segment_Display u_7_segment_display_3 (
    .g(hex_7_segment_decoder_2_out_1), .f(hex_7_segment_decoder_2_out_2), .a(hex_7_segment_decoder_2_out_3),
    .b(hex_7_segment_decoder_2_out_4), .e(hex_7_segment_decoder_2_out_5), .d(hex_7_segment_decoder_2_out_6),
    .c(hex_7_segment_decoder_2_out_7));  // open: dp
  _7_Segment_Display u_7_segment_display_4 (
    .g(hex_7_segment_decoder_1_out_1), .f(hex_7_segment_decoder_1_out_2), .a(hex_7_segment_decoder_1_out_3),
    .b(hex_7_segment_decoder_1_out_4), .e(hex_7_segment_decoder_1_out_5), .d(hex_7_segment_decoder_1_out_6),
    .c(hex_7_segment_decoder_1_out_7));  // open: dp
  and and_1 (and_1_out, B3, A3);
  xnor xnor_1 (xnor_1_out, A3, not_1_out[3]);
  and and_2 (and_2_out, xnor_1_out, not_3_out[3]);
  or or_1 (S, and_2_out, and_1_out);
  Four_bit_Subtractor four_bit_subtractor_1 (
    .A0(A0), .A1(A1), .A2(A2), .A3(1'b0), .B0(B0), .B1(B1), .B2(B2), .B3(1'b0),
    .Out1(four_bit_subtractor_1_out1[0]), .Out2(four_bit_subtractor_1_out1[1]),
    .Out3(four_bit_subtractor_1_out1[2]), .Out4(four_bit_subtractor_1_out1[3]),
    .Cout(four_bit_subtractor_1_cout));
  not not_1 (not_1_out[3], four_bit_subtractor_1_cout);
  Four_bit_Subtractor four_bit_subtractor_2 (
    .A0(B0), .A1(B1), .A2(B2), .A3(1'b0), .B0(A0), .B1(A1), .B2(A2), .B3(1'b0),
    .Out1(four_bit_subtractor_2_out1[0]), .Out2(four_bit_subtractor_2_out1[1]),
    .Out3(four_bit_subtractor_2_out1[2]), .Out4(four_bit_subtractor_2_out1[3]),
    .Cout(four_bit_subtractor_2_cout));
  not not_2 (not_2_out[3], four_bit_subtractor_2_cout);
  Four_bit_Adder four_bit_adder_1 (
    .A0(A0), .A1(A1), .A2(A2), .A3(1'b0), .B0(B0), .B1(B1), .B2(B2), .B3(1'b0),
    .Out1(four_bit_adder_1_out1[0]), .Out2(four_bit_adder_1_out1[1]), .Out3(four_bit_adder_1_out1[2]),
    .Out4(four_bit_adder_1_out1[3]));  // open: Cn, Cout
  _7_Segment_Display u_7_segment_display_5 ();  // open: g, f, a, b, e, d, c, dp
  _7_Segment_Display u_7_segment_display_6 ();  // open: g, f, a, b, e, d, c, dp
  assign and_3_out = four_bit_subtractor_1_out1 & {4{not_1_out[3]}};  // AND_Gate and_3, 4 bits wide
  assign and_4_out = four_bit_subtractor_2_out1 & {4{not_2_out[3]}};  // AND_Gate and_4, 4 bits wide
  xnor xnor_2 (xnor_2_out[3], A3, B3);
  not not_3 (not_3_out[3], xnor_2_out[3]);
  assign or_2_out = and_3_out | and_4_out;  // OR_Gate or_2, 4 bits wide
  assign and_5_out = four_bit_adder_1_out1 & {4{xnor_2_out[3]}};  // AND_Gate and_5, 4 bits wide
  assign and_6_out = {4{not_3_out[3]}} & or_2_out;  // AND_Gate and_6, 4 bits wide
  assign or_3_out = and_5_out | and_6_out;  // OR_Gate or_3, 4 bits wide
  Hex_7_segment_decoder hex_7_segment_decoder_3 (
    .in_1(or_3_out[0]), .in_2(or_3_out[1]), .in_3(or_3_out[2]), .in_4(or_3_out[3]), .Out_1(Out1),
    .Out_2(Out2), .Out_3(Out3), .Out_4(Out4), .Out_5(Out5), .Out_6(Out6), .Out_7(Out7));
endmodule

module One_complement_Adder (
  input  A0,
  input  A1,
  input  A2,
  input  A3,
  input  B0,
  input  B1,
  input  B2,
  input  B3,
  input  in_9,
  input  in_10,
  input  in_11,
  input  in_12,
  input  in_13,
  input  in_14,
  input  in_15,
  input  in_16
);

  wire hex_7_segment_decoder_1_out_1, hex_7_segment_decoder_1_out_2, hex_7_segment_decoder_1_out_3,
       hex_7_segment_decoder_1_out_4, hex_7_segment_decoder_1_out_5, hex_7_segment_decoder_1_out_6,
       hex_7_segment_decoder_1_out_7, multiplexer_3_bit_2_to_1_1_out1, multiplexer_3_bit_2_to_1_1_out2,
       multiplexer_3_bit_2_to_1_1_out3, multiplexer_3_bit_2_to_1_2_out1, multiplexer_3_bit_2_to_1_2_out2,
       multiplexer_3_bit_2_to_1_2_out3, multiplexer_3_bit_2_to_1_3_out1, multiplexer_3_bit_2_to_1_3_out2,
       multiplexer_3_bit_2_to_1_3_out3, not_1_out, not_2_out, not_3_out, not_4_out, not_5_out, not_6_out,
       not_8_out, not_9_out, not_10_out, sign_and_magnitude_adder_1_out1, sign_and_magnitude_adder_1_out2,
       sign_and_magnitude_adder_1_out3, sign_and_magnitude_adder_1_out4, sign_and_magnitude_adder_1_out5,
       sign_and_magnitude_adder_1_out6, sign_and_magnitude_adder_1_out7, sign_and_magnitude_adder_1_s;
  wire [3:0] and_1_out, and_2_out, four_bit_adder_1_out1, four_bit_adder_2_out1, or_1_out;
  wire [3:3] four_bit_adder_1_cn, not_7_out;

  not not_1 (not_1_out, A0);
  not not_2 (not_2_out, A1);
  not not_3 (not_3_out, A2);
  not not_4 (not_4_out, B0);
  not not_5 (not_5_out, B1);
  not not_6 (not_6_out, B2);
  Multiplexer_3_bit_2_to_1 multiplexer_3_bit_2_to_1_1 (
    .A0(not_1_out), .A1(not_2_out), .A2(not_3_out), .B0(A0), .B1(A1), .B2(A2), .S(A3),
    .Out1(multiplexer_3_bit_2_to_1_1_out1), .Out2(multiplexer_3_bit_2_to_1_1_out2),
    .Out3(multiplexer_3_bit_2_to_1_1_out3));
  Multiplexer_3_bit_2_to_1 multiplexer_3_bit_2_to_1_2 (
    .A0(not_4_out), .A1(not_5_out), .A2(not_6_out), .B0(B0), .B1(B1), .B2(B2), .S(B3),
    .Out1(multiplexer_3_bit_2_to_1_2_out1), .Out2(multiplexer_3_bit_2_to_1_2_out2),
    .Out3(multiplexer_3_bit_2_to_1_2_out3));
  Four_bit_Adder four_bit_adder_1 (
    .A0(in_9), .A1(in_10), .A2(in_11), .A3(in_12), .B0(in_13), .B1(in_14), .B2(in_15), .B3(in_16),
    .Cn(four_bit_adder_1_cn[3]), .Out1(four_bit_adder_1_out1[0]), .Out2(four_bit_adder_1_out1[1]),
    .Out3(four_bit_adder_1_out1[2]), .Out4(four_bit_adder_1_out1[3]));  // open: Cout
  Sign_and_magnitude_Adder sign_and_magnitude_adder_1 (
    .A0(multiplexer_3_bit_2_to_1_1_out1), .A1(multiplexer_3_bit_2_to_1_1_out2),
    .A2(multiplexer_3_bit_2_to_1_1_out3), .A3(A3), .B0(multiplexer_3_bit_2_to_1_2_out1),
    .B1(multiplexer_3_bit_2_to_1_2_out2), .B2(multiplexer_3_bit_2_to_1_2_out3), .B3(B3),
    .Out1(sign_and_magnitude_adder_1_out1), .Out2(sign_and_magnitude_adder_1_out2),
    .Out3(sign_and_magnitude_adder_1_out3), .Out4(sign_and_magnitude_adder_1_out4),
    .S(sign_and_magnitude_adder_1_s), .Out5(sign_and_magnitude_adder_1_out5),
    .Out6(sign_and_magnitude_adder_1_out6), .Out7(sign_and_magnitude_adder_1_out7));
  Four_bit_Adder four_bit_adder_2 (
    .A0(four_bit_adder_1_out1[0]), .A1(four_bit_adder_1_out1[1]), .A2(four_bit_adder_1_out1[2]),
    .A3(four_bit_adder_1_out1[3]), .B0(1'b1), .B1(1'b0), .B2(1'b0), .B3(1'b0),
    .Out1(four_bit_adder_2_out1[0]), .Out2(four_bit_adder_2_out1[1]), .Out3(four_bit_adder_2_out1[2]),
    .Out4(four_bit_adder_2_out1[3]));  // open: Cn, Cout
  not not_7 (not_7_out[3], four_bit_adder_1_cn[3]);
  _7_Segment_Display u_7_segment_display_1 (.g(sign_and_magnitude_adder_1_s));  // open: f, a, b, e, d, c, dp
  assign and_1_out = {4{not_7_out[3]}} & four_bit_adder_1_out1;  // AND_Gate and_1, 4 bits wide
  assign and_2_out = {4{four_bit_adder_1_cn[3]}} & four_bit_adder_2_out1;  // AND_Gate and_2, 4 bits wide
  _7_Segment_Display u_7_segment_display_2 (
    .g(sign_and_magnitude_adder_1_out1), .f(sign_and_magnitude_adder_1_out2),
    .a(sign_and_magnitude_adder_1_out3), .b(sign_and_magnitude_adder_1_out4),
    .e(sign_and_magnitude_adder_1_out5), .d(sign_and_magnitude_adder_1_out6),
    .c(sign_and_magnitude_adder_1_out7));  // open: dp
  assign or_1_out = and_1_out | and_2_out;  // OR_Gate or_1, 4 bits wide
  not not_8 (not_8_out, or_1_out[0]);
  not not_9 (not_9_out, or_1_out[1]);
  not not_10 (not_10_out, or_1_out[2]);
  Multiplexer_3_bit_2_to_1 multiplexer_3_bit_2_to_1_3 (
    .A0(not_8_out), .A1(not_9_out), .A2(not_10_out), .B0(or_1_out[0]), .B1(or_1_out[1]), .B2(or_1_out[2]),
    .S(or_1_out[3]), .Out1(multiplexer_3_bit_2_to_1_3_out1), .Out2(multiplexer_3_bit_2_to_1_3_out2),
    .Out3(multiplexer_3_bit_2_to_1_3_out3));
  Hex_7_segment_decoder hex_7_segment_decoder_1 (
    .in_1(multiplexer_3_bit_2_to_1_3_out1), .in_2(multiplexer_3_bit_2_to_1_3_out2),
    .in_3(multiplexer_3_bit_2_to_1_3_out3), .in_4(1'b0), .Out_1(hex_7_segment_decoder_1_out_1),
    .Out_2(hex_7_segment_decoder_1_out_2), .Out_3(hex_7_segment_decoder_1_out_3),
    .Out_4(hex_7_segment_decoder_1_out_4), .Out_5(hex_7_segment_decoder_1_out_5),
    .Out_6(hex_7_segment_decoder_1_out_6), .Out_7(hex_7_segment_decoder_1_out_7));
  _7_Segment_Display u_7_segment_display_3 (.g(or_1_out[3]));  // open: f, a, b, e, d, c, dp
  _7_Segment_Display u_7_segment_display_4 (
    .g(hex_7_segment_decoder_1_out_1), .f(hex_7_segment_decoder_1_out_2), .a(hex_7_segment_decoder_1_out_3),
    .b(hex_7_segment_decoder_1_out_4), .e(hex_7_segment_decoder_1_out_5), .d(hex_7_segment_decoder_1_out_6),
    .c(hex_7_segment_decoder_1_out_7));  // open: dp
endmodule

module Two_complement_Adder (
  input  in_1,
  input  in_2,
  input  in_3,
  input  in_4,
  input  in_5,
  input  in_6,
  input  in_7,
  input  in_8
);

  wire four_bit_adder_1_cn, four_bit_adder_1_cout, four_bit_adder_1_out1, four_bit_adder_1_out2,
       four_bit_adder_1_out3, four_bit_adder_1_out4, two_complement_decoder_1_out1,
       two_complement_decoder_1_out2, two_complement_decoder_1_out3, two_complement_decoder_1_out4,
       two_complement_decoder_1_out5, two_complement_decoder_1_out6, two_complement_decoder_1_out7,
       two_complement_decoder_1_s, two_complement_decoder_2_out1, two_complement_decoder_2_out2,
       two_complement_decoder_2_out3, two_complement_decoder_2_out4, two_complement_decoder_2_out5,
       two_complement_decoder_2_out6, two_complement_decoder_2_out7, two_complement_decoder_2_s,
       two_complement_decoder_3_out1, two_complement_decoder_3_out2, two_complement_decoder_3_out3,
       two_complement_decoder_3_out4, two_complement_decoder_3_out5, two_complement_decoder_3_out6,
       two_complement_decoder_3_out7, two_complement_decoder_3_s, xor_1_out;

  Two_complement_Decoder two_complement_decoder_1 (
    .in_1(in_1), .in_2(in_2), .in_3(in_3), .in_4(in_4), .Out1(two_complement_decoder_1_out1),
    .Out2(two_complement_decoder_1_out2), .Out3(two_complement_decoder_1_out3),
    .Out4(two_complement_decoder_1_out4), .Out5(two_complement_decoder_1_out5),
    .Out6(two_complement_decoder_1_out6), .Out7(two_complement_decoder_1_out7), .S(two_complement_decoder_1_s));
  Two_complement_Decoder two_complement_decoder_2 (
    .in_1(in_5), .in_2(in_6), .in_3(in_7), .in_4(in_8), .Out1(two_complement_decoder_2_out1),
    .Out2(two_complement_decoder_2_out2), .Out3(two_complement_decoder_2_out3),
    .Out4(two_complement_decoder_2_out4), .Out5(two_complement_decoder_2_out5),
    .Out6(two_complement_decoder_2_out6), .Out7(two_complement_decoder_2_out7), .S(two_complement_decoder_2_s));
  Four_bit_Adder four_bit_adder_1 (
    .A0(in_1), .A1(in_2), .A2(in_3), .A3(in_4), .B0(in_5), .B1(in_6), .B2(in_7), .B3(in_8),
    .Cn(four_bit_adder_1_cn), .Out1(four_bit_adder_1_out1), .Out2(four_bit_adder_1_out2),
    .Out3(four_bit_adder_1_out3), .Out4(four_bit_adder_1_out4), .Cout(four_bit_adder_1_cout));
  _7_Segment_Display u_7_segment_display_1 (
    .g(two_complement_decoder_1_out1), .f(two_complement_decoder_1_out2), .a(two_complement_decoder_1_out3),
    .b(two_complement_decoder_1_out4), .e(two_complement_decoder_1_out5), .d(two_complement_decoder_1_out6),
    .c(two_complement_decoder_1_out7));  // open: dp
  _7_Segment_Display u_7_segment_display_2 (.g(two_complement_decoder_1_s));  // open: f, a, b, e, d, c, dp
  _7_Segment_Display u_7_segment_display_3 (
    .g(two_complement_decoder_2_out1), .f(two_complement_decoder_2_out2), .a(two_complement_decoder_2_out3),
    .b(two_complement_decoder_2_out4), .e(two_complement_decoder_2_out5), .d(two_complement_decoder_2_out6),
    .c(two_complement_decoder_2_out7));  // open: dp
  _7_Segment_Display u_7_segment_display_4 (.g(two_complement_decoder_2_s));  // open: f, a, b, e, d, c, dp
  Two_complement_Decoder two_complement_decoder_3 (
    .in_1(four_bit_adder_1_out1), .in_2(four_bit_adder_1_out2), .in_3(four_bit_adder_1_out3),
    .in_4(four_bit_adder_1_out4), .Out1(two_complement_decoder_3_out1), .Out2(two_complement_decoder_3_out2),
    .Out3(two_complement_decoder_3_out3), .Out4(two_complement_decoder_3_out4),
    .Out5(two_complement_decoder_3_out5), .Out6(two_complement_decoder_3_out6),
    .Out7(two_complement_decoder_3_out7), .S(two_complement_decoder_3_s));
  _7_Segment_Display u_7_segment_display_5 (.g(two_complement_decoder_3_s));  // open: f, a, b, e, d, c, dp
  _7_Segment_Display u_7_segment_display_6 (
    .g(two_complement_decoder_3_out1), .f(two_complement_decoder_3_out2), .a(two_complement_decoder_3_out3),
    .b(two_complement_decoder_3_out4), .e(two_complement_decoder_3_out5), .d(two_complement_decoder_3_out6),
    .c(two_complement_decoder_3_out7));  // open: dp
  xor xor_1 (xor_1_out, four_bit_adder_1_cn, four_bit_adder_1_cout);
  _7_Segment_Display u_7_segment_display_7 (
    .g(xor_1_out), .f(xor_1_out), .a(xor_1_out), .e(xor_1_out), .d(xor_1_out));  // open: b, c, dp
endmodule

module Two_complement_Decoder (
  input  in_1,
  input  in_2,
  input  in_3,
  input  in_4,
  output Out1,
  output Out2,
  output Out3,
  output Out4,
  output Out5,
  output Out6,
  output Out7,
  output S
);

  wire four_bit_adder_1_out1, four_bit_adder_1_out2, four_bit_adder_1_out3, four_bit_adder_1_out4;
  wire [3:0] not_1_out;
  wire [6:0] and_1_out, and_2_out, hex_7_segment_decoder_1_out_1, hex_7_segment_decoder_2_out_1, not_2_out;

  assign not_1_out = ~{in_4, in_3, in_2, in_1};  // NOT_Gate not_1, 4 bits wide
  assign not_2_out = ~{7{in_4}};  // NOT_Gate not_2, 7 bits wide
  Hex_7_segment_decoder hex_7_segment_decoder_1 (
    .in_1(in_1), .in_2(in_2), .in_3(in_3), .in_4(in_4), .Out_1(hex_7_segment_decoder_1_out_1[0]),
    .Out_2(hex_7_segment_decoder_1_out_1[1]), .Out_3(hex_7_segment_decoder_1_out_1[2]),
    .Out_4(hex_7_segment_decoder_1_out_1[3]), .Out_5(hex_7_segment_decoder_1_out_1[4]),
    .Out_6(hex_7_segment_decoder_1_out_1[5]), .Out_7(hex_7_segment_decoder_1_out_1[6]));
  Four_bit_Adder four_bit_adder_1 (
    .A0(not_1_out[0]), .A1(not_1_out[1]), .A2(not_1_out[2]), .A3(not_1_out[3]), .B0(1'b1), .B1(1'b0),
    .B2(1'b0), .B3(1'b0), .Out1(four_bit_adder_1_out1), .Out2(four_bit_adder_1_out2),
    .Out3(four_bit_adder_1_out3), .Out4(four_bit_adder_1_out4));  // open: Cn, Cout
  Hex_7_segment_decoder hex_7_segment_decoder_2 (
    .in_1(four_bit_adder_1_out1), .in_2(four_bit_adder_1_out2), .in_3(four_bit_adder_1_out3),
    .in_4(four_bit_adder_1_out4), .Out_1(hex_7_segment_decoder_2_out_1[0]),
    .Out_2(hex_7_segment_decoder_2_out_1[1]), .Out_3(hex_7_segment_decoder_2_out_1[2]),
    .Out_4(hex_7_segment_decoder_2_out_1[3]), .Out_5(hex_7_segment_decoder_2_out_1[4]),
    .Out_6(hex_7_segment_decoder_2_out_1[5]), .Out_7(hex_7_segment_decoder_2_out_1[6]));
  assign and_1_out = hex_7_segment_decoder_1_out_1 & not_2_out;  // AND_Gate and_1, 7 bits wide
  assign and_2_out = {7{in_4}} & hex_7_segment_decoder_2_out_1;  // AND_Gate and_2, 7 bits wide
  assign {Out7, Out6, Out5, Out4, Out3, Out2, Out1} = and_1_out | and_2_out;  // OR_Gate or_1, 7 bits wide

  assign S = in_4;
endmodule
