// Logisim project Sequential_Logic_Circuit.circ as structural Verilog: 7 circuits, main circuit D_latch
module D_latch (
  input  rst,
  input  WE,
  input  D,
  output Q1,
  output Q2
);

  wire and_1_out, and_2_out, not_1_out, not_2_out;

  not not_1 (not_1_out, D);
  not not_2 (not_2_out, rst);
  and and_1 (and_1_out, not_1_out, WE);
  and and_2 (and_2_out, WE, not_2_out, D);
  nor nor_1 (Q1, and_1_out, rst, Q2);
  nor nor_2 (Q2, Q1, and_2_out);
endmodule

module D_Flip_Flop (
  input  EN,
  input  Rst,
  input  Clk,
  input  D,
  output Q1,
  output Q2
);

  wire and_1_out, d_latch_1_q1, not_1_out;

  not not_1 (not_1_out, Clk);
  and and_1 (and_1_out, EN, Clk);
  D_latch d_latch_1 (.rst(Rst), .WE(not_1_out), .D(D), .Q1(d_latch_1_q1));  // open: Q2
  D_latch d_latch_2 (.rst(Rst), .WE(and_1_out), .D(d_latch_1_q1), .Q1(Q1), .Q2(Q2));
endmodule

module Four_bit_Register (
  input  D0,
  input  D1,
  input  D2,
  input  D3,
  input  EN,
  input  clk,
  input  Rst,
  output out_8,
  output out_9,
  output out_10,
  output out_11
);

  D_Flip_Flop d_flip_flop_1 (.Clk(clk), .D(D0), .EN(EN), .Rst(Rst), .Q1(out_8));  // open: Q2
  D_Flip_Flop d_flip_flop_2 (.Clk(clk), .D(D1), .EN(EN), .Rst(Rst), .Q1(out_9));  // open: Q2
  D_Flip_Flop d_flip_flop_3 (.Clk(clk), .D(D2), .EN(EN), .Rst(Rst), .Q1(out_10));  // open: Q2
  D_Flip_Flop d_flip_flop_4 (.Clk(clk), .D(D3), .EN(EN), .Rst(Rst), .Q1(out_11));  // open: Q2
endmodule

module Four_bit_Counter (
  input  EN,
  input  clk,
  input  Rst,
  output Out1,
  output Out2,
  output Out3,
  output Out4
);

  wire four_bit_adder_1_out1, four_bit_adder_1_out2, four_bit_adder_1_out3, four_bit_adder_1_out4,
       hex_7_segment_decoder_1_out_1, hex_7_segment_decoder_1_out_2, hex_7_segment_decoder_1_out_3,
       hex_7_segment_decoder_1_out_4, hex_7_segment_decoder_1_out_5, hex_7_segment_decoder_1_out_6,
       hex_7_segment_decoder_1_out_7;

  Four_bit_Register four_bit_register_1 (
    .D0(four_bit_adder_1_out1), .D1(four_bit_adder_1_out2), .D2(four_bit_adder_1_out3),
    .D3(four_bit_adder_1_out4), .EN(EN), .clk(clk), .Rst(Rst), .out_8(Out1), .out_9(Out2), .out_10(Out3),
    .out_11(Out4));
  Four_bit_Adder four_bit_adder_1 (
    .A0(Out1), .A1(Out2), .A2(Out3), .A3(Out4), .B0(1'b1), .Out1(four_bit_adder_1_out1),
    .Out2(four_bit_adder_1_out2), .Out3(four_bit_adder_1_out3), .Out4(four_bit_adder_1_out4));  // open: B1, B2, B3, Cn, Cout
  Hex_7_segment_decoder hex_7_segment_decoder_1 (
    .Out_1(hex_7_segment_decoder_1_out_1), .Out_2(hex_7_segment_decoder_1_out_2),
    .Out_3(hex_7_segment_decoder_1_out_3), .Out_4(hex_7_segment_decoder_1_out_4),
    .Out_5(hex_7_segment_decoder_1_out_5), .Out_6(hex_7_segment_decoder_1_out_6),
    .Out_7(hex_7_segment_decoder_1_out_7));  // open: in_1, in_2, in_3, in_4
  _7_Segment_Display u_7_segment_display_1 (
    .g(hex_7_segment_decoder_1_out_1), .f(hex_7_segment_decoder_1_out_2), .a(hex_7_segment_decoder_1_out_3),
    .b(hex_7_segment_decoder_1_out_4), .e(hex_7_segment_decoder_1_out_5), .d(hex_7_segment_decoder_1_out_6),
    .c(hex_7_segment_decoder_1_out_7));  // open: dp
endmodule

module Eight_bit_Register (
  input  D0,
  input  D1,
  input  D2,
  input  D3,
  input  D4,
  input  D5,
  input  D6,
  input  D7,
  input  EN,
  input  clk,
  input  Rst,
  output out_12,
  output out_13,
  output out_14,
  output out_15,
  output out_16,
  output out_17,
  output out_18,
  output out_19
);

  D_Flip_Flop d_flip_flop_1 (.Clk(clk), .D(D0), .EN(EN), .Rst(Rst), .Q1(out_12));  // open: Q2
  D_Flip_Flop d_flip_flop_2 (.Clk(clk), .D(D1), .EN(EN), .Rst(Rst), .Q1(out_13));  // open: Q2
  D_Flip_Flop d_flip_flop_3 (.Clk(clk), .D(D2), .EN(EN), .Rst(Rst), .Q1(out_14));  // open: Q2
  D_Flip_Flop d_flip_flop_4 (.Clk(clk), .D(D3), .EN(EN), .Rst(Rst), .Q1(out_15));  // open: Q2
  D_Flip_Flop d_flip_flop_5 (.Clk(clk), .D(D4), .EN(EN), .Rst(Rst), .Q1(out_16));  // open: Q2
  D_Flip_Flop d_flip_flop_6 (.Clk(clk), .D(D5), .EN(EN), .Rst(Rst), .Q1(out_17));  // open: Q2
  D_Flip_Flop d_flip_flop_7 (.Clk(clk), .D(D6), .EN(EN), .Rst(Rst), .Q1(out_18));  // open: Q2
  D_Flip_Flop d_flip_flop_8 (.Clk(clk), .D(D7), .EN(EN), .Rst(Rst), .Q1(out_19));  // open: Q2
endmodule

module Sum (
  output out_1,
  output out_2,
  output out_3,
  output out_4,
  output out_5,
  output out_6,
  output out_7,
  output out_8
);

  wire button_1_out, button_2_out, eight_bit_adder_1_out1, eight_bit_adder_1_out2, eight_bit_adder_1_out3,
       eight_bit_adder_1_out4, eight_bit_adder_1_out5, eight_bit_adder_1_out6, eight_bit_adder_1_out7,
       eight_bit_adder_1_out8, eight_bit_adder_2_out1, eight_bit_adder_2_out2, eight_bit_adder_2_out3,
       eight_bit_adder_2_out4, eight_bit_adder_2_out5, eight_bit_adder_2_out6, eight_bit_adder_2_out7,
       eight_bit_adder_2_out8, eight_bit_register_2_out_12, eight_bit_register_2_out_13,
       eight_bit_register_2_out_14, eight_bit_register_2_out_15, eight_bit_register_2_out_16,
       eight_bit_register_2_out_17, eight_bit_register_2_out_18, eight_bit_register_2_out_19;

  Button button_1 (.out(button_1_out));
  Button button_2 (.out(button_2_out));
  Eight_bit_Register eight_bit_register_1 (
    .D0(eight_bit_adder_1_out1), .D1(eight_bit_adder_1_out2), .D2(eight_bit_adder_1_out3),
    .D3(eight_bit_adder_1_out4), .D4(eight_bit_adder_1_out5), .D5(eight_bit_adder_1_out6),
    .D6(eight_bit_adder_1_out7), .D7(eight_bit_adder_1_out8), .EN(1'b1), .clk(button_1_out),
    .Rst(button_2_out), .out_12(out_1), .out_13(out_2), .out_14(out_3), .out_15(out_4), .out_16(out_5),
    .out_17(out_6), .out_18(out_7), .out_19(out_8));
  Eight_bit_Register eight_bit_register_2 (
    .D0(eight_bit_adder_2_out1), .D1(eight_bit_adder_2_out2), .D2(eight_bit_adder_2_out3),
    .D3(eight_bit_adder_2_out4), .D4(eight_bit_adder_2_out5), .D5(eight_bit_adder_2_out6),
    .D6(eight_bit_adder_2_out7), .D7(eight_bit_adder_2_out8), .EN(1'b1), .clk(button_1_out),
    .Rst(button_2_out), .out_12(eight_bit_register_2_out_12), .out_13(eight_bit_register_2_out_13),
    .out_14(eight_bit_register_2_out_14), .out_15(eight_bit_register_2_out_15),
    .out_16(eight_bit_register_2_out_16), .out_17(eight_bit_register_2_out_17),
    .out_18(eight_bit_register_2_out_18), .out_19(eight_bit_register_2_out_19));
  Eight_bit_Adder eight_bit_adder_1 (
    .A0(out_1), .A1(out_2), .A2(out_3), .A3(out_4), .A4(out_5), .A5(out_6), .A6(out_7), .A7(out_8),
    .B0(eight_bit_register_2_out_12), .B1(eight_bit_register_2_out_13), .B2(eight_bit_register_2_out_14),
    .B3(eight_bit_register_2_out_15), .B4(eight_bit_register_2_out_16), .B5(eight_bit_register_2_out_17),
    .B6(eight_bit_register_2_out_18), .B7(eight_bit_register_2_out_19), .Out1(eight_bit_adder_1_out1),
    .Out2(eight_bit_adder_1_out2), .Out3(eight_bit_adder_1_out3), .Out4(eight_bit_adder_1_out4),
    .Out5(eight_bit_adder_1_out5), .Out6(eight_bit_adder_1_out6), .Out7(eight_bit_adder_1_out7),
    .Out8(eight_bit_adder_1_out8));  // open: Cn, Cout
  Eight_bit_Adder eight_bit_adder_2 (
    .A0(eight_bit_register_2_out_12), .A1(eight_bit_register_2_out_13), .A2(eight_bit_register_2_out_14),
    .A3(eight_bit_register_2_out_15), .A4(eight_bit_register_2_out_16), .A5(eight_bit_register_2_out_17),
    .A6(eight_bit_register_2_out_18), .A7(eight_bit_register_2_out_19), .B0(1'b1),
    .Out1(eight_bit_adder_2_out1), .Out2(eight_bit_adder_2_out2), .Out3(eight_bit_adder_2_out3),
    .Out4(eight_bit_adder_2_out4), .Out5(eight_bit_adder_2_out5), .Out6(eight_bit_adder_2_out6),
    .Out7(eight_bit_adder_2_out7), .Out8(eight_bit_adder_2_out8));  // open: B1, B2, B3, B4, B5, B6, B7, Cn, Cout
endmodule

module Electronic_Clock (
  input  in_1
);

  wire and_1_out, and_2_out, button_1_out, clock_1_out, four_bit_adder_1_out1, four_bit_adder_1_out2,
       four_bit_adder_1_out3, four_bit_adder_1_out4, four_bit_adder_2_out1, four_bit_adder_2_out2,
       four_bit_adder_2_out3, four_bit_adder_2_out4, four_bit_counter_1_out1, four_bit_counter_1_out2,
       four_bit_counter_1_out3, four_bit_counter_1_out4, four_bit_register_1_out_8,
       four_bit_register_1_out_9, four_bit_register_1_out_10, four_bit_register_1_out_11,
       four_bit_register_2_out_8, four_bit_register_2_out_9, four_bit_register_2_out_10,
       four_bit_register_2_out_11, hex_7_segment_decoder_1_out_1, hex_7_segment_decoder_1_out_2,
       hex_7_segment_decoder_1_out_3, hex_7_segment_decoder_1_out_4, hex_7_segment_decoder_1_out_5,
       hex_7_segment_decoder_1_out_6, hex_7_segment_decoder_1_out_7, hex_7_segment_decoder_2_out_1,
       hex_7_segment_decoder_2_out_2, hex_7_segment_decoder_2_out_3, hex_7_segment_decoder_2_out_4,
       hex_7_segment_decoder_2_out_5, hex_7_segment_decoder_2_out_6, hex_7_segment_decoder_2_out_7,
       hex_7_segment_decoder_3_out_1, hex_7_segment_decoder_3_out_2, hex_7_segment_decoder_3_out_3,
       hex_7_segment_decoder_3_out_4, hex_7_segment_decoder_3_out_5, hex_7_segment_decoder_3_out_6,
       hex_7_segment_decoder_3_out_7, not_1_out, not_2_out, not_3_out, or_1_out, or_2_out;

  Clock clock_1 (.out(clock_1_out));
  Button button_1 (.out(button_1_out));
  or or_1 (or_1_out, button_1_out, and_2_out);
  Four_bit_Register four_bit_register_1 (
    .D0(four_bit_adder_1_out1), .D1(four_bit_adder_1_out2), .D2(four_bit_adder_1_out3),
    .D3(four_bit_adder_1_out4), .EN(in_1), .clk(and_1_out), .Rst(or_1_out),
    .out_8(four_bit_register_1_out_8), .out_9(four_bit_register_1_out_9),
    .out_10(four_bit_register_1_out_10), .out_11(four_bit_register_1_out_11));
  or or_2 (or_2_out, and_1_out, button_1_out);
  Four_bit_Counter four_bit_counter_1 (
    .EN(in_1), .clk(clock_1_out), .Rst(or_2_out), .Out1(four_bit_counter_1_out1),
    .Out2(four_bit_counter_1_out2), .Out3(four_bit_counter_1_out3), .Out4(four_bit_counter_1_out4));
  Hex_7_segment_decoder hex_7_segment_decoder_1 (
    .in_1(four_bit_register_1_out_8), .in_2(four_bit_register_1_out_9), .in_3(four_bit_register_1_out_10),
    .in_4(four_bit_register_1_out_11), .Out_1(hex_7_segment_decoder_1_out_1),
    .Out_2(hex_7_segment_decoder_1_out_2), .Out_3(hex_7_segment_decoder_1_out_3),
    .Out_4(hex_7_segment_decoder_1_out_4), .Out_5(hex_7_segment_decoder_1_out_5),
    .Out_6(hex_7_segment_decoder_1_out_6), .Out_7(hex_7_segment_decoder_1_out_7));
  Four_bit_Adder four_bit_adder_1 (
    .A0(four_bit_register_1_out_8), .A1(four_bit_register_1_out_9), .A2(four_bit_register_1_out_10),
    .A3(four_bit_register_1_out_11), .B0(1'b1), .Out1(four_bit_adder_1_out1), .Out2(four_bit_adder_1_out2),
    .Out3(four_bit_adder_1_out3), .Out4(four_bit_adder_1_out4));  // open: B1, B2, B3, Cn, Cout
  and and_1 (and_1_out, hex_7_segment_decoder_2_out_1, hex_7_segment_decoder_2_out_2, hex_7_segment_decoder_2_out_3, hex_7_segment_decoder_2_out_4, hex_7_segment_decoder_2_out_5, not_1_out, hex_7_segment_decoder_2_out_7);
  Four_bit_Register four_bit_register_2 (
    .D0(four_bit_adder_2_out1), .D1(four_bit_adder_2_out2), .D2(four_bit_adder_2_out3),
    .D3(four_bit_adder_2_out4), .EN(in_1), .clk(and_2_out), .Rst(button_1_out),
    .out_8(four_bit_register_2_out_8), .out_9(four_bit_register_2_out_9),
    .out_10(four_bit_register_2_out_10), .out_11(four_bit_register_2_out_11));
  not not_1 (not_1_out, hex_7_segment_decoder_2_out_6);
  Hex_7_segment_decoder hex_7_segment_decoder_2 (
    .in_1(four_bit_counter_1_out1), .in_2(four_bit_counter_1_out2), .in_3(four_bit_counter_1_out3),
    .in_4(four_bit_counter_1_out4), .Out_1(hex_7_segment_decoder_2_out_1),
    .Out_2(hex_7_segment_decoder_2_out_2), .Out_3(hex_7_segment_decoder_2_out_3),
    .Out_4(hex_7_segment_decoder_2_out_4), .Out_5(hex_7_segment_decoder_2_out_5),
    .Out_6(hex_7_segment_decoder_2_out_6), .Out_7(hex_7_segment_decoder_2_out_7));
  and and_2 (and_2_out, not_2_out, hex_7_segment_decoder_2_out_2, hex_7_segment_decoder_2_out_3, hex_7_segment_decoder_2_out_4, hex_7_segment_decoder_2_out_5, hex_7_segment_decoder_2_out_6, hex_7_segment_decoder_2_out_7, hex_7_segment_decoder_1_out_1, hex_7_segment_decoder_1_out_2, hex_7_segment_decoder_1_out_3, not_3_out, hex_7_segment_decoder_1_out_5, hex_7_segment_decoder_1_out_6, hex_7_segment_decoder_1_out_7);
  not not_2 (not_2_out, hex_7_segment_decoder_2_out_1);
  Hex_7_segment_decoder hex_7_segment_decoder_3 (
    .in_1(four_bit_register_2_out_8), .in_2(four_bit_register_2_out_9), .in_3(four_bit_register_2_out_10),
    .in_4(four_bit_register_2_out_11), .Out_1(hex_7_segment_decoder_3_out_1),
    .Out_2(hex_7_segment_decoder_3_out_2), .Out_3(hex_7_segment_decoder_3_out_3),
    .Out_4(hex_7_segment_decoder_3_out_4), .Out_5(hex_7_segment_decoder_3_out_5),
    .Out_6(hex_7_segment_decoder_3_out_6), .Out_7(hex_7_segment_decoder_3_out_7));
  Four_bit_Adder four_bit_adder_2 (
    .A0(four_bit_register_2_out_8), .A1(four_bit_register_2_out_9), .A2(four_bit_register_2_out_10),
    .A3(four_bit_register_2_out_11), .B0(1'b1), .Out1(four_bit_adder_2_out1), .Out2(four_bit_adder_2_out2),
    .Out3(four_bit_adder_2_out3), .Out4(four_bit_adder_2_out4));  // open: B1, B2, B3, Cn, Cout
  _7_Segment_Display u_7_segment_display_1 (
    .g(hex_7_segment_decoder_3_out_1), .f(hex_7_segment_decoder_3_out_2), .a(hex_7_segment_decoder_3_out_3),
    .b(hex_7_segment_decoder_3_out_4), .e(hex_7_segment_decoder_3_out_5), .d(hex_7_segment_decoder_3_out_6),
    .c(hex_7_segment_decoder_3_out_7));  // open: dp
  not not_3 (not_3_out, hex_7_segment_decoder_1_out_4);
  _7_Segment_Display u_7_segment_display_2 (
    .g(hex_7_segment_decoder_1_out_1), .f(hex_7_segment_decoder_1_out_2), .a(hex_7_segment_decoder_1_out_3),
    .b(hex_7_segment_decoder_1_out_4), .e(hex_7_segment_decoder_1_out_5), .d(hex_7_segment_decoder_1_out_6),
    .c(hex_7_segment_decoder_1_out_7));  // open: dp
  _7_Segment_Display u_7_segment_display_3 (
    .g(hex_7_segment_decoder_2_out_1), .f(hex_7_segment_decoder_2_out_2), .a(hex_7_segment_decoder_2_out_3),
    .b(hex_7_segment_decoder_2_out_4), .e(hex_7_segment_decoder_2_out_5), .d(hex_7_segment_decoder_2_out_6),
    .c(hex_7_segment_decoder_2_out_7));  // open: dp
endmodule
