// Logisim project UP_D_Flip_Flop.circ as structural Verilog: 4 circuits, main circuit Up_D_flip_flop
module Up_D_flip_flop (
  input  EN,
  input  Rst,
  input  Clk,
  input  D,
  output Q1,
  output Q2
);

  wire and_1_out, dd_latch_1_q1, not_1_out;

  not not_1 (not_1_out, Clk);
  and and_1 (and_1_out, EN, not_1_out);
  DD_latch dd_latch_1 (.rst(Rst), .WE(Clk), .D(D), .Q1(dd_latch_1_q1));  // open: Q2
  DD_latch dd_latch_2 (.rst(Rst), .WE(and_1_out), .D(dd_latch_1_q1), .Q1(Q1), .Q2(Q2));
endmodule

module Up_Four_Bit_Register (
  input  D0,
  input  D1,
  input  D2,
  input  D3,
  input  EN,
  input  clk,
  input  Rst,
  output out_8,
  output out_9,
  output out_10,
  output out_11
);

  Up_D_flip_flop up_d_flip_flop_1 (.Clk(clk), .EN(EN), .D(D0), .Rst(Rst), .Q1(out_8));  // open: Q2
  Up_D_flip_flop up_d_flip_flop_2 (.Clk(clk), .EN(EN), .D(D1), .Rst(Rst), .Q1(out_9));  // open: Q2
  Up_D_flip_flop up_d_flip_flop_3 (.Clk(clk), .EN(EN), .D(D2), .Rst(Rst), .Q1(out_10));  // open: Q2
  Up_D_flip_flop up_d_flip_flop_4 (.Clk(clk), .EN(EN), .D(D3), .Rst(Rst), .Q1(out_11));  // open: Q2
endmodule

module Up_Four_Bit_Counter (
  input  EN,
  input  clk,
  input  Rst,
  output Out1,
  output Out2,
  output Out3,
  output Out4
);

  wire four_bit_adder_1_out1, four_bit_adder_1_out2, four_bit_adder_1_out3, four_bit_adder_1_out4;

  Up_Four_Bit_Register up_four_bit_register_1 (
    .D0(four_bit_adder_1_out1), .D1(four_bit_adder_1_out2), .D2(four_bit_adder_1_out3),
    .D3(four_bit_adder_1_out4), .EN(EN), .clk(clk), .Rst(Rst), .out_8(Out1), .out_9(Out2), .out_10(Out3),
    .out_11(Out4));
  Four_bit_Adder four_bit_adder_1 (
    .A0(Out1), .A1(Out2), .A2(Out3), .A3(Out4), .B0(1'b1), .Out1(four_bit_adder_1_out1),
    .Out2(four_bit_adder_1_out2), .Out3(four_bit_adder_1_out3), .Out4(four_bit_adder_1_out4));  // open: B1, B2, B3, Cn, Cout
endmodule

module DD_latch (
  input  rst,
  input  WE,
  input  D,
  output Q1,
  output Q2
);

  wire and_1_out, and_2_out, not_1_out, not_2_out;

  not not_1 (not_1_out, D);
  not not_2 (not_2_out, rst);
  and and_1 (and_1_out, not_1_out, WE);
  and and_2 (and_2_out, WE, not_2_out, D);
  nor nor_1 (Q1, and_1_out, rst, Q2);
  nor nor_2 (Q2, Q1, and_2_out);
endmodule
