// Logisim project XOR_and_XNOR_Gates.circ as structural Verilog: 1 circuit, main circuit main
module main (
  input  in_1,
  input  in_2,
  input  in_3,
  input  in_4,
  input  in_5,
  input  in_6
);

  wire and_1_out, and_2_out, and_3_out, nand_1_out, nand_2_out, nor_1_out, nor_2_out, not_1_out, not_2_out,
       or_1_out, or_2_out;

  not not_1 (not_1_out, in_2);
  not not_2 (not_2_out, in_1);
  and and_1 (and_1_out, in_1, not_1_out);
  and and_2 (and_2_out, not_2_out, in_2);
  and and_3 (and_3_out, in_3, in_4);
  nand nand_1 (nand_1_out, in_5, in_6);
  or or_1 (or_1_out, in_5, in_6);
  or or_2 (or_2_out, and_1_out, and_2_out);
  LED led_1 (.in(or_2_out));
  nor nor_1 (nor_1_out, in_3, in_4);
  nor nor_2 (nor_2_out, nor_1_out, and_3_out);
  LED led_2 (.in(nor_2_out));
  nand nand_2 (nand_2_out, nand_1_out, or_1_out);
  LED led_3 (.in(nand_2_out));
endmodule
