// Logisim project sCPU.circ as structural Verilog: 6 circuits, main circuit main
module main (
  input  EN,
  input  D5,
  input  D6,
  input  D7,
  input  D8
);

  wire and_1_out, and_3_out, and_4_out, and_6_out, and_7_out, and_8_out, and_9_out, button_1_out,
       clock_1_out, comparator_8_bit_1_out_17, hex_7_segment_decoder_1_out_1, hex_7_segment_decoder_1_out_2,
       hex_7_segment_decoder_1_out_3, hex_7_segment_decoder_1_out_4, hex_7_segment_decoder_1_out_5,
       hex_7_segment_decoder_1_out_6, hex_7_segment_decoder_1_out_7, hex_7_segment_decoder_2_out_1,
       hex_7_segment_decoder_2_out_2, hex_7_segment_decoder_2_out_3, hex_7_segment_decoder_2_out_4,
       hex_7_segment_decoder_2_out_5, hex_7_segment_decoder_2_out_6, hex_7_segment_decoder_2_out_7,
       not_1_out, not_2_out, or_1_out, or_2_out, pc_register_1_out1, pc_register_1_out2, pc_register_1_out3,
       pc_register_1_out4, rom_8_8_1_out5, rom_8_8_1_out6, rom_8_8_1_out7, rom_8_8_1_out8;
  wire [3:0] and_24_out, rom_8_8_1_out1;
  wire [3:3] Opcode_out_1;
  wire [7:0] and_2_out, and_5_out, and_10_out, and_11_out, and_12_out, and_13_out, and_14_out, and_15_out,
       and_16_out, and_17_out, and_18_out, and_19_out, and_20_out, and_21_out, and_22_out, and_23_out,
       eight_bit_adder_1_out1, eight_bit_register_1_out_12, eight_bit_register_2_out_12,
       eight_bit_register_3_out_12, eight_bit_register_4_out_12, or_3_out, or_4_out, or_5_out, or_6_out;
  wire [7:7] decoder_2_4_1_out_0, decoder_2_4_1_out_1, decoder_2_4_1_out_2, decoder_2_4_1_out_3,
       decoder_2_4_2_out_0, decoder_2_4_2_out_1, decoder_2_4_2_out_2, decoder_2_4_2_out_3,
       decoder_2_4_3_out_0, decoder_2_4_3_out_1, decoder_2_4_3_out_2, decoder_2_4_3_out_3, Opcode_out_0,
       Opcode_out_2, Opcode_out_3;

  not not_1 (not_1_out, Opcode_out_1[3]);
  not not_2 (not_2_out, Opcode_out_3[7]);
  or or_1 (or_1_out, comparator_8_bit_1_out_17, not_2_out);
  and and_1 (and_1_out, not_1_out, or_1_out);
  Clock clock_1 (.out(clock_1_out));
  Button button_1 (.out(button_1_out));
  Hex_7_segment_decoder hex_7_segment_decoder_1 (
    .in_1(pc_register_1_out1), .in_2(pc_register_1_out2), .in_3(pc_register_1_out3),
    .in_4(pc_register_1_out4), .Out_1(hex_7_segment_decoder_1_out_1), .Out_2(hex_7_segment_decoder_1_out_2),
    .Out_3(hex_7_segment_decoder_1_out_3), .Out_4(hex_7_segment_decoder_1_out_4),
    .Out_5(hex_7_segment_decoder_1_out_5), .Out_6(hex_7_segment_decoder_1_out_6),
    .Out_7(hex_7_segment_decoder_1_out_7));
  PC_Register pc_register_1 (
    .addr0(rom_8_8_1_out1[2]), .addr1(rom_8_8_1_out1[3]), .addr2(rom_8_8_1_out5), .addr3(rom_8_8_1_out6),
    .flag(and_1_out), .EN(EN), .clk(clock_1_out), .Rst(button_1_out), .Out1(pc_register_1_out1),
    .Out2(pc_register_1_out2), .Out3(pc_register_1_out3), .Out4(pc_register_1_out4));
  _7_Segment_Display u_7_segment_display_1 (
    .g(hex_7_segment_decoder_1_out_1), .f(hex_7_segment_decoder_1_out_2), .a(hex_7_segment_decoder_1_out_3),
    .b(hex_7_segment_decoder_1_out_4), .e(hex_7_segment_decoder_1_out_5), .d(hex_7_segment_decoder_1_out_6),
    .c(hex_7_segment_decoder_1_out_7));  // open: dp
  ROM_8_8 rom_8_8_1 (
    .in_1(pc_register_1_out1), .in_2(pc_register_1_out2), .in_3(pc_register_1_out3),
    .in_4(pc_register_1_out4), .Out1(rom_8_8_1_out1[0]), .Out2(rom_8_8_1_out1[1]), .Out3(rom_8_8_1_out1[2]),
    .Out4(rom_8_8_1_out1[3]), .Out5(rom_8_8_1_out5), .Out6(rom_8_8_1_out6), .Out7(rom_8_8_1_out7),
    .Out8(rom_8_8_1_out8));
  assign and_2_out = {8{Opcode_out_0[7]}} & eight_bit_adder_1_out1;  // AND_Gate and_2, 8 bits wide
  and and_3 (and_3_out, Opcode_out_0[7], EN);
  Decoder_2_4 Opcode (
    .In_0(rom_8_8_1_out7), .In_1(rom_8_8_1_out8), .Out_0(Opcode_out_0[7]), .Out_1(Opcode_out_1[3]),
    .Out_2(Opcode_out_2[7]), .Out_3(Opcode_out_3[7]));
  and and_4 (and_4_out, Opcode_out_2[7], EN);
  assign and_5_out = {8{Opcode_out_2[7]}} & {D8, D7, D6, D5, rom_8_8_1_out1};  // AND_Gate and_5, 8 bits wide
  or or_2 (or_2_out, and_3_out, and_4_out);
  assign or_3_out = and_5_out | and_2_out;  // OR_Gate or_3, 8 bits wide
  Decoder_2_4 decoder_2_4_1 (
    .In_0(rom_8_8_1_out5), .In_1(rom_8_8_1_out6), .Out_0(decoder_2_4_1_out_0[7]),
    .Out_1(decoder_2_4_1_out_1[7]), .Out_2(decoder_2_4_1_out_2[7]), .Out_3(decoder_2_4_1_out_3[7]));
  and and_6 (and_6_out, decoder_2_4_1_out_0[7], or_2_out);
  and and_7 (and_7_out, decoder_2_4_1_out_1[7], or_2_out);
  and and_8 (and_8_out, decoder_2_4_1_out_2[7], or_2_out);
  and and_9 (and_9_out, decoder_2_4_1_out_3[7], or_2_out);
  Decoder_2_4 decoder_2_4_2 (
    .In_0(rom_8_8_1_out1[2]), .In_1(rom_8_8_1_out1[3]), .Out_0(decoder_2_4_2_out_0[7]),
    .Out_1(decoder_2_4_2_out_1[7]), .Out_2(decoder_2_4_2_out_2[7]), .Out_3(decoder_2_4_2_out_3[7]));
  assign and_10_out = {8{decoder_2_4_1_out_2[7]}} & or_3_out;  // AND_Gate and_10, 8 bits wide
  assign and_11_out = or_3_out & {8{decoder_2_4_1_out_3[7]}};  // AND_Gate and_11, 8 bits wide
  assign and_12_out = {8{decoder_2_4_1_out_0[7]}} & or_3_out;  // AND_Gate and_12, 8 bits wide
  assign and_13_out = {8{decoder_2_4_1_out_1[7]}} & or_3_out;  // AND_Gate and_13, 8 bits wide
  Decoder_2_4 decoder_2_4_3 (
    .In_0(rom_8_8_1_out1[0]), .In_1(rom_8_8_1_out1[1]), .Out_0(decoder_2_4_3_out_0[7]),
    .Out_1(decoder_2_4_3_out_1[7]), .Out_2(decoder_2_4_3_out_2[7]), .Out_3(decoder_2_4_3_out_3[7]));
  Eight_bit_Register eight_bit_register_1 (
    .D0(and_12_out[0]), .D1(and_12_out[1]), .D2(and_12_out[2]), .D3(and_12_out[3]), .D4(and_12_out[4]),
    .D5(and_12_out[5]), .D6(and_12_out[6]), .D7(and_12_out[7]), .EN(and_6_out), .clk(clock_1_out),
    .Rst(button_1_out), .out_12(eight_bit_register_1_out_12[0]), .out_13(eight_bit_register_1_out_12[1]),
    .out_14(eight_bit_register_1_out_12[2]), .out_15(eight_bit_register_1_out_12[3]),
    .out_16(eight_bit_register_1_out_12[4]), .out_17(eight_bit_register_1_out_12[5]),
    .out_18(eight_bit_register_1_out_12[6]), .out_19(eight_bit_register_1_out_12[7]));
  Eight_bit_Register eight_bit_register_2 (
    .D0(and_13_out[0]), .D1(and_13_out[1]), .D2(and_13_out[2]), .D3(and_13_out[3]), .D4(and_13_out[4]),
    .D5(and_13_out[5]), .D6(and_13_out[6]), .D7(and_13_out[7]), .EN(and_7_out), .clk(clock_1_out),
    .Rst(button_1_out), .out_12(eight_bit_register_2_out_12[0]), .out_13(eight_bit_register_2_out_12[1]),
    .out_14(eight_bit_register_2_out_12[2]), .out_15(eight_bit_register_2_out_12[3]),
    .out_16(eight_bit_register_2_out_12[4]), .out_17(eight_bit_register_2_out_12[5]),
    .out_18(eight_bit_register_2_out_12[6]), .out_19(eight_bit_register_2_out_12[7]));
  Eight_bit_Register eight_bit_register_3 (
    .D0(and_10_out[0]), .D1(and_10_out[1]), .D2(and_10_out[2]), .D3(and_10_out[3]), .D4(and_10_out[4]),
    .D5(and_10_out[5]), .D6(and_10_out[6]), .D7(and_10_out[7]), .EN(and_8_out), .clk(clock_1_out),
    .Rst(button_1_out), .out_12(eight_bit_register_3_out_12[0]), .out_13(eight_bit_register_3_out_12[1]),
    .out_14(eight_bit_register_3_out_12[2]), .out_15(eight_bit_register_3_out_12[3]),
    .out_16(eight_bit_register_3_out_12[4]), .out_17(eight_bit_register_3_out_12[5]),
    .out_18(eight_bit_register_3_out_12[6]), .out_19(eight_bit_register_3_out_12[7]));
  Eight_bit_Register eight_bit_register_4 (
    .D0(and_11_out[0]), .D1(and_11_out[1]), .D2(and_11_out[2]), .D3(and_11_out[3]), .D4(and_11_out[4]),
    .D5(and_11_out[5]), .D6(and_11_out[6]), .D7(and_11_out[7]), .EN(and_9_out), .clk(clock_1_out),
    .Rst(button_1_out), .out_12(eight_bit_register_4_out_12[0]), .out_13(eight_bit_register_4_out_12[1]),
    .out_14(eight_bit_register_4_out_12[2]), .out_15(eight_bit_register_4_out_12[3]),
    .out_16(eight_bit_register_4_out_12[4]), .out_17(eight_bit_register_4_out_12[5]),
    .out_18(eight_bit_register_4_out_12[6]), .out_19(eight_bit_register_4_out_12[7]));
  assign and_14_out = {8{decoder_2_4_3_out_0[7]}} & eight_bit_register_1_out_12;  // AND_Gate and_14, 8 bits wide
  assign and_15_out = {8{decoder_2_4_3_out_1[7]}} & eight_bit_register_2_out_12;  // AND_Gate and_15, 8 bits wide
  assign and_16_out = {8{decoder_2_4_3_out_2[7]}} & eight_bit_register_3_out_12;  // AND_Gate and_16, 8 bits wide
  assign and_17_out = {8{decoder_2_4_3_out_3[7]}} & eight_bit_register_4_out_12;  // AND_Gate and_17, 8 bits wide
  assign and_18_out = eight_bit_register_1_out_12 & {8{decoder_2_4_2_out_0[7]}};  // AND_Gate and_18, 8 bits wide
  assign and_19_out = eight_bit_register_2_out_12 & {8{decoder_2_4_2_out_1[7]}};  // AND_Gate and_19, 8 bits wide
  assign and_20_out = eight_bit_register_3_out_12 & {8{decoder_2_4_2_out_2[7]}};  // AND_Gate and_20, 8 bits wide
  assign and_21_out = eight_bit_register_4_out_12 & {8{decoder_2_4_2_out_3[7]}};  // AND_Gate and_21, 8 bits wide
  assign or_4_out = and_18_out | and_19_out | and_20_out | and_21_out;  // OR_Gate or_4, 8 bits wide
  assign or_5_out = and_14_out | and_15_out | and_16_out | and_17_out;  // OR_Gate or_5, 8 bits wide
  assign and_22_out = or_4_out & {8{Opcode_out_0[7]}};  // AND_Gate and_22, 8 bits wide
  assign and_23_out = {8{Opcode_out_3[7]}} & eight_bit_register_1_out_12;  // AND_Gate and_23, 8 bits wide
  assign or_6_out = and_23_out | and_22_out;  // OR_Gate or_6, 8 bits wide
  Eight_bit_Adder eight_bit_adder_1 (
    .A0(or_5_out[0]), .A1(or_5_out[1]), .A2(or_5_out[2]), .A3(or_5_out[3]), .A4(or_5_out[4]),
    .A5(or_5_out[5]), .A6(or_5_out[6]), .A7(or_5_out[7]), .B0(or_6_out[0]), .B1(or_6_out[1]),
    .B2(or_6_out[2]), .B3(or_6_out[3]), .B4(or_6_out[4]), .B5(or_6_out[5]), .B6(or_6_out[6]),
    .B7(or_6_out[7]), .Out1(eight_bit_adder_1_out1[0]), .Out2(eight_bit_adder_1_out1[1]),
    .Out3(eight_bit_adder_1_out1[2]), .Out4(eight_bit_adder_1_out1[3]), .Out5(eight_bit_adder_1_out1[4]),
    .Out6(eight_bit_adder_1_out1[5]), .Out7(eight_bit_adder_1_out1[6]), .Out8(eight_bit_adder_1_out1[7]));  // open: Cn, Cout
  Comparator_8_bit comparator_8_bit_1 (
    .A0(or_5_out[0]), .A1(or_5_out[1]), .A2(or_5_out[2]), .A3(or_5_out[3]), .A4(or_5_out[4]),
    .A5(or_5_out[5]), .A6(or_5_out[6]), .A7(or_5_out[7]), .B0(or_6_out[0]), .B1(or_6_out[1]),
    .B2(or_6_out[2]), .B3(or_6_out[3]), .B4(or_6_out[4]), .B5(or_6_out[5]), .B6(or_6_out[6]),
    .B7(or_6_out[7]), .out_17(comparator_8_bit_1_out_17));
  assign and_24_out = {4{Opcode_out_1[3]}} & or_5_out[3:0];  // AND_Gate and_24, 4 bits wide
  Hex_7_segment_decoder hex_7_segment_decoder_2 (
    .in_1(and_24_out[0]), .in_2(and_24_out[1]), .in_3(and_24_out[2]), .in_4(and_24_out[3]),
    .Out_1(hex_7_segment_decoder_2_out_1), .Out_2(hex_7_segment_decoder_2_out_2),
    .Out_3(hex_7_segment_decoder_2_out_3), .Out_4(hex_7_segment_decoder_2_out_4),
    .Out_5(hex_7_segment_decoder_2_out_5), .Out_6(hex_7_segment_decoder_2_out_6),
    .Out_7(hex_7_segment_decoder_2_out_7));
  _7_Segment_Display u_7_segment_display_2 (
    .g(hex_7_segment_decoder_2_out_1), .f(hex_7_segment_decoder_2_out_2), .a(hex_7_segment_decoder_2_out_3),
    .b(hex_7_segment_decoder_2_out_4), .e(hex_7_segment_decoder_2_out_5), .d(hex_7_segment_decoder_2_out_6),
    .c(hex_7_segment_decoder_2_out_7));  // open: dp
endmodule

module ROM_3_8 (
  input  In_0,
  input  In_1,
  output Out1,
  output Out2,
  output Out3,
  output Out4,
  output Out5,
  output Out6,
  output Out7,
  output Out8
);

  wire and_1_out, and_2_out, and_3_out, and_4_out, and_5_out, and_6_out, and_7_out, and_8_out, and_9_out,
       and_10_out, and_11_out, and_12_out, and_13_out, and_14_out, and_15_out, and_16_out, and_17_out,
       and_18_out, and_19_out, and_20_out, and_21_out, and_22_out, and_23_out, and_24_out, and_25_out,
       and_26_out, and_27_out, and_28_out, and_29_out, and_30_out, and_31_out, and_32_out,
       decoder_2_4_1_out_0, decoder_2_4_1_out_1, decoder_2_4_1_out_2, decoder_2_4_1_out_3;

  Decoder_2_4 decoder_2_4_1 (
    .In_0(In_0), .In_1(In_1), .Out_0(decoder_2_4_1_out_0), .Out_1(decoder_2_4_1_out_1),
    .Out_2(decoder_2_4_1_out_2), .Out_3(decoder_2_4_1_out_3));
  and and_1 (and_1_out, 1'b1, decoder_2_4_1_out_0);
  and and_2 (and_2_out, decoder_2_4_1_out_1, 1'b1);
  and and_3 (and_3_out, 1'b1, decoder_2_4_1_out_2);
  and and_4 (and_4_out, decoder_2_4_1_out_3, 1'b1);
  or or_1 (Out8, and_4_out, and_3_out, and_2_out, and_1_out);
  and and_5 (and_5_out, 1'b0, decoder_2_4_1_out_0);
  and and_6 (and_6_out, decoder_2_4_1_out_1, 1'b0);
  and and_7 (and_7_out, 1'b0, decoder_2_4_1_out_2);
  and and_8 (and_8_out, decoder_2_4_1_out_3, 1'b0);
  or or_2 (Out7, and_8_out, and_7_out, and_6_out, and_5_out);
  and and_9 (and_9_out, 1'b0, decoder_2_4_1_out_0);
  and and_10 (and_10_out, decoder_2_4_1_out_1, 1'b0);
  and and_11 (and_11_out, 1'b1, decoder_2_4_1_out_2);
  and and_12 (and_12_out, decoder_2_4_1_out_3, 1'b1);
  or or_3 (Out6, and_12_out, and_11_out, and_10_out, and_9_out);
  and and_13 (and_13_out, 1'b0, decoder_2_4_1_out_0);
  and and_14 (and_14_out, decoder_2_4_1_out_1, 1'b1);
  and and_15 (and_15_out, 1'b0, decoder_2_4_1_out_2);
  and and_16 (and_16_out, decoder_2_4_1_out_3, 1'b1);
  or or_4 (Out5, and_16_out, and_15_out, and_14_out, and_13_out);
  and and_17 (and_17_out, 1'b1, decoder_2_4_1_out_0);
  and and_18 (and_18_out, decoder_2_4_1_out_1, 1'b0);
  and and_19 (and_19_out, 1'b0, decoder_2_4_1_out_2);
  and and_20 (and_20_out, decoder_2_4_1_out_3, 1'b0);
  or or_5 (Out4, and_20_out, and_19_out, and_18_out, and_17_out);
  and and_21 (and_21_out, 1'b0, decoder_2_4_1_out_0);
  and and_22 (and_22_out, decoder_2_4_1_out_1, 1'b0);
  and and_23 (and_23_out, 1'b0, decoder_2_4_1_out_2);
  and and_24 (and_24_out, decoder_2_4_1_out_3, 1'b0);
  or or_6 (Out3, and_24_out, and_23_out, and_22_out, and_21_out);
  and and_25 (and_25_out, 1'b1, decoder_2_4_1_out_0);
  and and_26 (and_26_out, decoder_2_4_1_out_1, 1'b0);
  and and_27 (and_27_out, 1'b0, decoder_2_4_1_out_2);
  and and_28 (and_28_out, decoder_2_4_1_out_3, 1'b0);
  or or_7 (Out2, and_28_out, and_27_out, and_26_out, and_25_out);
  and and_29 (and_29_out, 1'b0, decoder_2_4_1_out_0);
  and and_30 (and_30_out, decoder_2_4_1_out_1, 1'b0);
  and and_31 (and_31_out, 1'b0, decoder_2_4_1_out_2);
  and and_32 (and_32_out, decoder_2_4_1_out_3, 1'b1);
  or or_8 (Out1, and_32_out, and_31_out, and_30_out, and_29_out);
endmodule

module RAM_4_8 (
  input  In_0,
  input  In_1,
  input  clk,
  input  EN,
  input  Rst,
  input  D0,
  input  D1,
  input  D2,
  input  D3,
  input  D5,
  input  D6,
  input  D7,
  input  D8,
  output Out1,
  output Out2,
  output Out3,
  output Out4,
  output Out5,
  output Out6,
  output Out7,
  output Out8
);

  wire and_1_out, and_2_out, and_3_out, and_4_out;
  wire [7:0] and_5_out, and_6_out, and_7_out, and_8_out, and_9_out, and_10_out, and_11_out, and_12_out,
       eight_bit_register_1_out_12, eight_bit_register_2_out_12, eight_bit_register_3_out_12,
       eight_bit_register_4_out_12;
  wire [7:7] decoder_2_4_1_out_0, decoder_2_4_1_out_1, decoder_2_4_1_out_2, decoder_2_4_1_out_3;

  Decoder_2_4 decoder_2_4_1 (
    .In_0(In_0), .In_1(In_1), .Out_0(decoder_2_4_1_out_0[7]), .Out_1(decoder_2_4_1_out_1[7]),
    .Out_2(decoder_2_4_1_out_2[7]), .Out_3(decoder_2_4_1_out_3[7]));
  and and_1 (and_1_out, decoder_2_4_1_out_0[7], EN);
  and and_2 (and_2_out, decoder_2_4_1_out_1[7], EN);
  and and_3 (and_3_out, decoder_2_4_1_out_2[7], EN);
  and and_4 (and_4_out, decoder_2_4_1_out_3[7], EN);
  assign and_5_out = {8{decoder_2_4_1_out_2[7]}} & {D8, D7, D6, D5, D3, D2, D1, D0};  // AND_Gate and_5, 8 bits wide
  assign and_6_out = {D8, D7, D6, D5, D3, D2, D1, D0} & {8{decoder_2_4_1_out_3[7]}};  // AND_Gate and_6, 8 bits wide
  assign and_7_out = {8{decoder_2_4_1_out_0[7]}} & {D8, D7, D6, D5, D3, D2, D1, D0};  // AND_Gate and_7, 8 bits wide
  assign and_8_out = {8{decoder_2_4_1_out_1[7]}} & {D8, D7, D6, D5, D3, D2, D1, D0};  // AND_Gate and_8, 8 bits wide
  Eight_bit_Register eight_bit_register_1 (
    .D0(and_7_out[0]), .D1(and_7_out[1]), .D2(and_7_out[2]), .D3(and_7_out[3]), .D4(and_7_out[4]),
    .D5(and_7_out[5]), .D6(and_7_out[6]), .D7(and_7_out[7]), .EN(and_1_out), .clk(clk), .Rst(Rst),
    .out_12(eight_bit_register_1_out_12[0]), .out_13(eight_bit_register_1_out_12[1]),
    .out_14(eight_bit_register_1_out_12[2]), .out_15(eight_bit_register_1_out_12[3]),
    .out_16(eight_bit_register_1_out_12[4]), .out_17(eight_bit_register_1_out_12[5]),
    .out_18(eight_bit_register_1_out_12[6]), .out_19(eight_bit_register_1_out_12[7]));
  Eight_bit_Register eight_bit_register_2 (
    .D0(and_8_out[0]), .D1(and_8_out[1]), .D2(and_8_out[2]), .D3(and_8_out[3]), .D4(and_8_out[4]),
    .D5(and_8_out[5]), .D6(and_8_out[6]), .D7(and_8_out[7]), .EN(and_2_out), .clk(clk), .Rst(Rst),
    .out_12(eight_bit_register_2_out_12[0]), .out_13(eight_bit_register_2_out_12[1]),
    .out_14(eight_bit_register_2_out_12[2]), .out_15(eight_bit_register_2_out_12[3]),
    .out_16(eight_bit_register_2_out_12[4]), .out_17(eight_bit_register_2_out_12[5]),
    .out_18(eight_bit_register_2_out_12[6]), .out_19(eight_bit_register_2_out_12[7]));
  Eight_bit_Register eight_bit_register_3 (
    .D0(and_5_out[0]), .D1(and_5_out[1]), .D2(and_5_out[2]), .D3(and_5_out[3]), .D4(and_5_out[4]),
    .D5(and_5_out[5]), .D6(and_5_out[6]), .D7(and_5_out[7]), .EN(and_3_out), .clk(clk), .Rst(Rst),
    .out_12(eight_bit_register_3_out_12[0]), .out_13(eight_bit_register_3_out_12[1]),
    .out_14(eight_bit_register_3_out_12[2]), .out_15(eight_bit_register_3_out_12[3]),
    .out_16(eight_bit_register_3_out_12[4]), .out_17(eight_bit_register_3_out_12[5]),
    .out_18(eight_bit_register_3_out_12[6]), .out_19(eight_bit_register_3_out_12[7]));
  Eight_bit_Register eight_bit_register_4 (
    .D0(and_6_out[0]), .D1(and_6_out[1]), .D2(and_6_out[2]), .D3(and_6_out[3]), .D4(and_6_out[4]),
    .D5(and_6_out[5]), .D6(and_6_out[6]), .D7(and_6_out[7]), .EN(and_4_out), .clk(clk), .Rst(Rst),
    .out_12(eight_bit_register_4_out_12[0]), .out_13(eight_bit_register_4_out_12[1]),
    .out_14(eight_bit_register_4_out_12[2]), .out_15(eight_bit_register_4_out_12[3]),
    .out_16(eight_bit_register_4_out_12[4]), .out_17(eight_bit_register_4_out_12[5]),
    .out_18(eight_bit_register_4_out_12[6]), .out_19(eight_bit_register_4_out_12[7]));
  assign and_9_out = {8{decoder_2_4_1_out_0[7]}} & eight_bit_register_1_out_12;  // AND_Gate and_9, 8 bits wide
  assign and_10_out = {8{decoder_2_4_1_out_1[7]}} & eight_bit_register_2_out_12;  // AND_Gate and_10, 8 bits wide
  assign and_11_out = {8{decoder_2_4_1_out_2[7]}} & eight_bit_register_3_out_12;  // AND_Gate and_11, 8 bits wide
  assign and_12_out = {8{decoder_2_4_1_out_3[7]}} & eight_bit_register_4_out_12;  // AND_Gate and_12, 8 bits wide
  assign {Out8, Out7, Out6, Out5, Out4, Out3, Out2, Out1} = and_9_out | and_10_out | and_11_out | and_12_out;  // OR_Gate or_1, 8 bits wide
endmodule

module PC_Register (
  input  addr0,
  input  addr1,
  input  addr2,
  input  addr3,
  input  flag,
  input  EN,
  input  clk,
  input  Rst,
  output Out1,
  output Out2,
  output Out3,
  output Out4
);

  wire [3:0] and_1_out, and_2_out, four_bit_adder_1_out1, or_1_out;
  wire [3:3] not_1_out;

  not not_1 (not_1_out[3], flag);
  assign and_1_out = {addr3, addr2, addr1, addr0} & {4{not_1_out[3]}};  // AND_Gate and_1, 4 bits wide
  assign or_1_out = and_1_out | and_2_out;  // OR_Gate or_1, 4 bits wide
  assign and_2_out = {4{flag}} & four_bit_adder_1_out1;  // AND_Gate and_2, 4 bits wide
  Up_Four_Bit_Register up_four_bit_register_1 (
    .D0(or_1_out[0]), .D1(or_1_out[1]), .D2(or_1_out[2]), .D3(or_1_out[3]), .EN(EN), .clk(clk), .Rst(Rst),
    .out_8(Out1), .out_9(Out2), .out_10(Out3), .out_11(Out4));
  Four_bit_Adder four_bit_adder_1 (
    .A0(Out1), .A1(Out2), .A2(Out3), .A3(Out4), .B0(1'b1), .Out1(four_bit_adder_1_out1[0]),
    .Out2(four_bit_adder_1_out1[1]), .Out3(four_bit_adder_1_out1[2]), .Out4(four_bit_adder_1_out1[3]));  // open: B1, B2, B3, Cn, Cout
endmodule

module ROM_8_8 (
  input  in_1,
  input  in_2,
  input  in_3,
  input  in_4,
  output Out1,
  output Out2,
  output Out3,
  output Out4,
  output Out5,
  output Out6,
  output Out7,
  output Out8
);

  wire and_1_out, and_2_out, and_3_out, and_4_out, and_5_out, and_6_out, and_7_out, and_8_out, and_9_out,
       and_10_out, and_11_out, and_12_out, and_13_out, and_14_out, and_15_out, and_16_out, and_17_out,
       and_18_out, and_19_out, and_20_out, and_21_out, and_22_out, and_23_out, and_24_out, and_25_out,
       and_26_out, and_27_out, and_28_out, and_29_out, and_30_out, and_31_out, and_32_out, and_33_out,
       and_34_out, and_35_out, and_36_out, and_37_out, and_38_out, and_39_out, and_40_out, and_41_out,
       and_42_out, and_43_out, and_44_out, and_45_out, and_46_out, and_47_out, and_48_out, and_49_out,
       and_50_out, and_51_out, and_52_out, and_53_out, and_54_out, and_55_out, and_56_out, and_57_out,
       and_58_out, and_59_out, and_60_out, and_61_out, and_62_out, and_63_out, and_64_out,
       decoder_4_16_1_out_0, decoder_4_16_1_out_1, decoder_4_16_1_out_2, decoder_4_16_1_out_3,
       decoder_4_16_1_out_4, decoder_4_16_1_out_5, decoder_4_16_1_out_6, decoder_4_16_1_out_7;

  Decoder_4_16 decoder_4_16_1 (
    .In_0(in_1), .In_1(in_2), .In_2(in_3), .In_3(in_4), .Out_0(decoder_4_16_1_out_0),
    .Out_1(decoder_4_16_1_out_1), .Out_2(decoder_4_16_1_out_2), .Out_3(decoder_4_16_1_out_3),
    .Out_4(decoder_4_16_1_out_4), .Out_5(decoder_4_16_1_out_5), .Out_6(decoder_4_16_1_out_6),
    .Out_7(decoder_4_16_1_out_7));  // open: Out_8, Out_9, Out_10, Out_11, Out_12, Out_13, Out_14, Out_15
  and and_1 (and_1_out, 1'b1, decoder_4_16_1_out_0);
  and and_2 (and_2_out, decoder_4_16_1_out_1, 1'b1);
  and and_3 (and_3_out, 1'b1, decoder_4_16_1_out_2);
  and and_4 (and_4_out, decoder_4_16_1_out_3, 1'b1);
  and and_5 (and_5_out, 1'b0, decoder_4_16_1_out_4);
  and and_6 (and_6_out, decoder_4_16_1_out_5, 1'b0);
  and and_7 (and_7_out, 1'b1, decoder_4_16_1_out_6);
  and and_8 (and_8_out, decoder_4_16_1_out_7, 1'b0);
  or or_1 (Out8, and_8_out, and_7_out, and_6_out, and_5_out, and_4_out, and_3_out, and_2_out, and_1_out);
  and and_9 (and_9_out, 1'b0, decoder_4_16_1_out_0);
  and and_10 (and_10_out, decoder_4_16_1_out_1, 1'b0);
  and and_11 (and_11_out, 1'b0, decoder_4_16_1_out_2);
  and and_12 (and_12_out, decoder_4_16_1_out_3, 1'b0);
  and and_13 (and_13_out, 1'b0, decoder_4_16_1_out_4);
  and and_14 (and_14_out, decoder_4_16_1_out_5, 1'b0);
  and and_15 (and_15_out, 1'b1, decoder_4_16_1_out_6);
  and and_16 (and_16_out, decoder_4_16_1_out_7, 1'b1);
  or or_2 (Out7, and_16_out, and_15_out, and_14_out, and_13_out, and_12_out, and_11_out, and_10_out, and_9_out);
  and and_17 (and_17_out, 1'b0, decoder_4_16_1_out_0);
  and and_18 (and_18_out, decoder_4_16_1_out_1, 1'b0);
  and and_19 (and_19_out, 1'b1, decoder_4_16_1_out_2);
  and and_20 (and_20_out, decoder_4_16_1_out_3, 1'b1);
  and and_21 (and_21_out, 1'b1, decoder_4_16_1_out_4);
  and and_22 (and_22_out, decoder_4_16_1_out_5, 1'b0);
  and and_23 (and_23_out, 1'b0, decoder_4_16_1_out_6);
  and and_24 (and_24_out, decoder_4_16_1_out_7, 1'b0);
  or or_3 (Out6, and_24_out, and_23_out, and_22_out, and_21_out, and_20_out, and_19_out, and_18_out, and_17_out);
  and and_25 (and_25_out, 1'b0, decoder_4_16_1_out_0);
  and and_26 (and_26_out, decoder_4_16_1_out_1, 1'b1);
  and and_27 (and_27_out, 1'b0, decoder_4_16_1_out_2);
  and and_28 (and_28_out, decoder_4_16_1_out_3, 1'b1);
  and and_29 (and_29_out, 1'b0, decoder_4_16_1_out_4);
  and and_30 (and_30_out, decoder_4_16_1_out_5, 1'b1);
  and and_31 (and_31_out, 1'b1, decoder_4_16_1_out_6);
  and and_32 (and_32_out, decoder_4_16_1_out_7, 1'b1);
  or or_4 (Out5, and_32_out, and_31_out, and_30_out, and_29_out, and_28_out, and_27_out, and_26_out, and_25_out);
  and and_33 (and_33_out, 1'b0, decoder_4_16_1_out_0);
  and and_34 (and_34_out, decoder_4_16_1_out_1, 1'b0);
  and and_35 (and_35_out, 1'b0, decoder_4_16_1_out_2);
  and and_36 (and_36_out, decoder_4_16_1_out_3, 1'b0);
  and and_37 (and_37_out, 1'b1, decoder_4_16_1_out_4);
  and and_38 (and_38_out, decoder_4_16_1_out_5, 1'b0);
  and and_39 (and_39_out, 1'b0, decoder_4_16_1_out_6);
  and and_40 (and_40_out, decoder_4_16_1_out_7, 1'b1);
  or or_5 (Out4, and_40_out, and_39_out, and_38_out, and_37_out, and_36_out, and_35_out, and_34_out, and_33_out);
  and and_41 (and_41_out, 1'b0, decoder_4_16_1_out_6);
  and and_42 (and_42_out, decoder_4_16_1_out_7, 1'b1);
  and and_43 (and_43_out, 1'b1, decoder_4_16_1_out_0);
  and and_44 (and_44_out, decoder_4_16_1_out_1, 1'b0);
  and and_45 (and_45_out, 1'b0, decoder_4_16_1_out_2);
  and and_46 (and_46_out, decoder_4_16_1_out_3, 1'b0);
  and and_47 (and_47_out, 1'b0, decoder_4_16_1_out_4);
  and and_48 (and_48_out, decoder_4_16_1_out_5, 1'b1);
  or or_6 (Out3, and_42_out, and_41_out, and_48_out, and_47_out, and_46_out, and_45_out, and_44_out, and_43_out);
  and and_49 (and_49_out, 1'b1, decoder_4_16_1_out_0);
  and and_50 (and_50_out, decoder_4_16_1_out_1, 1'b0);
  and and_51 (and_51_out, 1'b0, decoder_4_16_1_out_2);
  and and_52 (and_52_out, decoder_4_16_1_out_3, 1'b1);
  and and_53 (and_53_out, 1'b0, decoder_4_16_1_out_4);
  and and_54 (and_54_out, decoder_4_16_1_out_5, 1'b1);
  and and_55 (and_55_out, 1'b0, decoder_4_16_1_out_6);
  and and_56 (and_56_out, decoder_4_16_1_out_7, 1'b1);
  or or_7 (Out2, and_56_out, and_55_out, and_54_out, and_53_out, and_52_out, and_51_out, and_50_out, and_49_out);
  and and_57 (and_57_out, 1'b1, decoder_4_16_1_out_0);
  and and_58 (and_58_out, decoder_4_16_1_out_1, 1'b1);
  and and_59 (and_59_out, 1'b0, decoder_4_16_1_out_2);
  and and_60 (and_60_out, decoder_4_16_1_out_3, 1'b0);
  and and_61 (and_61_out, 1'b1, decoder_4_16_1_out_4);
  and and_62 (and_62_out, decoder_4_16_1_out_5, 1'b1);
  and and_63 (and_63_out, 1'b1, decoder_4_16_1_out_6);
  and and_64 (and_64_out, decoder_4_16_1_out_7, 1'b0);
  or or_8 (Out1, and_64_out, and_63_out, and_62_out, and_61_out, and_60_out, and_59_out, and_58_out, and_57_out);
endmodule

module test (
  input  rst,
  input  WE,
  input  D,
  output Q1,
  output Q2
);

  wire and_1_out, and_2_out, not_1_out, not_2_out;

  not not_1 (not_1_out, D);
  not not_2 (not_2_out, rst);
  and and_1 (and_1_out, not_1_out, WE);
  and and_2 (and_2_out, WE, not_2_out, D);
  nor nor_1 (Q1, and_1_out, rst, Q2);
  nor nor_2 (Q2, Q1, and_2_out);
endmodule
